// Digital circuit DigLo66_Quiz1__02.dig as structural Verilog
module DigLo66_Quiz1__02 (
  input  [2:0] in0,
  input  [2:0] in1,
  input  addsubtract,
  output [2:0] out
);

  wire [1:0] add_1_s, bitcount_1_out, bitcount_2_out, sub_1_s;
  wire [2:2] add_1_c_o, sub_1_c_o;

  BitCount #(.Bits(3)) bitcount_1 (.in(in0), .out(bitcount_1_out));
  BitCount #(.Bits(3)) bitcount_2 (.in(in1), .out(bitcount_2_out));
  Add #(.Bits(2)) add_1 (.a(bitcount_2_out), .b(bitcount_1_out), .c_i(1'b0), .s(add_1_s), .c_o(add_1_c_o[2]));
  Sub #(.Bits(2)) sub_1 (.a(bitcount_1_out), .b(bitcount_2_out), .c_i(1'b0), .s(sub_1_s), .c_o(sub_1_c_o[2]));
  Multiplexer #(.Bits(3)) multiplexer_1 (
    .sel(addsubtract), .in_0({add_1_c_o[2], add_1_s}), .in_1({sub_1_c_o[2], sub_1_s}), .out(out));
endmodule
