// Digital circuit DigLo68_Exam1__2.dig as structural Verilog
module DigLo68_Exam1__2 (
  input  X3,
  input  X2,
  input  X1,
  input  X0,
  output Z3,
  output Z2,
  output Z1,
  output Z0
);

  wire and_1_out, and_2_out, and_3_out, and_4_out, and_5_out, and_6_out, and_7_out, and_8_out, and_9_out,
       and_10_out, and_11_out, and_12_out, and_13_out, and_14_out, not_1_out, not_2_out, not_3_out;

  not not_1 (not_1_out, X3);
  not not_2 (not_2_out, X2);
  not not_3 (not_3_out, X1);
  not not_4 (Z2, X0);
  and and_1 (and_1_out, X0, X1, not_2_out);
  and and_2 (and_2_out, X0, not_3_out, X2);
  and and_3 (and_3_out, X0, X1, not_1_out);
  and and_4 (and_4_out, X1, not_2_out, not_1_out);
  and and_5 (and_5_out, Z2, not_3_out, not_2_out, not_1_out);
  and and_6 (and_6_out, X0, X1, not_2_out, not_1_out);
  and and_7 (and_7_out, Z2, X1, X2, not_1_out);
  and and_8 (and_8_out, X0, not_3_out, not_2_out, X3);
  and and_9 (and_9_out, Z2, not_3_out, X2, X3);
  and and_10 (and_10_out, X0, X1, X2, X3);
  and and_11 (and_11_out, Z2, not_3_out, not_2_out, not_1_out);
  and and_12 (and_12_out, X0, not_3_out, X2, not_1_out);
  and and_13 (and_13_out, Z2, X1, not_2_out, X3);
  and and_14 (and_14_out, X0, X1, X2, X3);
  or or_1 (Z3, and_1_out, and_2_out, and_3_out, and_4_out);
  or or_2 (Z1, and_5_out, and_6_out, and_7_out, and_8_out, and_9_out, and_10_out);
  or or_3 (Z0, and_11_out, and_12_out, and_13_out, and_14_out);

  // Notes on the sheet:
  //   Z3: Is prime number?
  //   Z2: Is it divisible by 2?
  //   Z1: Is it divisible by 3?
  //   Z0: Is it divisible by 5?
  //   Don't change anything inside this box
endmodule

/* Test case T1:
X3 X2 X1 X0 Z3 Z2 Z1 Z0
0 0 0 0 0 1 1 1
0 1 1 1 1 0 0 0
1 0 1 0 0 1 0 1
*/
