// Digital circuit fulladdress2.dig as structural Verilog
module fulladdress2 (
  input  A,
  input  B,
  input  Cin,
  output out_4,
  output out_5
);

  wire Cin_t, N2, N3, N5, N6, N7, X;

  _7400 _7400_1 (
    .pin1(A), .pin2(B), .pin3(Cin), .pin4(A), .pin5(Cin), .pin6(N2), .pin7(1'b0), .pin8(N3), .pin9(B),
    .pin10(Cin), .pin11(X), .pin12(N2), .pin13(N3), .pin14(1'b1));
  _7400 _7400_2 (
    .pin1(X), .pin2(Cin_t), .pin3(N5), .pin4(X), .pin5(N5), .pin6(N6), .pin7(1'b0), .pin8(N7), .pin9(Cin_t),
    .pin10(N5), .pin11(out_4), .pin12(N6), .pin13(N7), .pin14(1'b1));
  _7400 _7400_3 (
    .pin1(Cin), .pin2(N5), .pin3(out_5), .pin4(1'b0), .pin5(1'b0), .pin7(1'b0), .pin9(1'b0), .pin10(1'b0),
    .pin12(1'b0), .pin13(1'b0), .pin14(1'b1));  // open: pin6, pin8, pin11

  // Other names for the same wires on the sheet: Cout = out_5; N1 = Cin; Sum = out_4
endmodule
