// Digital circuit Template-02.dig as structural Verilog
module Template_02 (
  input  [2:0] In,
  input  clk,
  output [7:0] Z
);

  wire i1__i2, i1__i2__i3, i1__i2_i3, i1_i2__i3, i1_i2_i3, i1_i2_i3_t, i2__i3, i2__i3_t, not_1_out,
       not_2_out, not_3_out;

  not not_1 (not_1_out, In[2]);
  not not_2 (not_2_out, In[1]);
  not not_3 (not_3_out, In[0]);
  and and_1 (i1__i2__i3, In[2], not_2_out, not_3_out);
  and and_2 (i1__i2_i3, not_1_out, not_2_out, In[0]);
  and and_3 (i1_i2_i3_t, In[2], In[1], In[0]);
  and and_4 (i1_i2__i3, not_1_out, In[1], not_3_out);
  and and_5 (i1_i2_i3, not_1_out, In[1], In[0]);
  and and_6 (i1__i2, In[2], not_2_out);
  and and_7 (i2__i3, not_2_out, not_3_out);
  and and_8 (i2__i3_t, In[1], not_3_out);
  or or_1 (Z[6], i1_i2_i3, i1_i2_i3_t, i2__i3, i1__i2_i3, i1__i2, i2__i3_t);
  or or_2 (Z[5], i1__i2__i3, i1_i2_i3_t, i1__i2_i3, i2__i3_t);
  or or_3 (Z[3], i1_i2_i3, i1__i2_i3, i1__i2);
  or or_4 (Z[2], i1_i2__i3, i1_i2_i3, i2__i3, i1__i2);
  or or_5 (Z[1], i1_i2__i3, i1__i2__i3, i1_i2_i3_t);
  or or_6 (Z[0], i1__i2__i3, i1__i2_i3, i2__i3_t);
  Terminal terminal_1 (.D({1'b0, Z[6:5], 1'b0, Z[3:0]}), .C(clk), .en(1'b1));

  assign {Z[7], Z[4]} = 2'b00;

  // Other names for the same wires on the sheet: B = Z[6]; C = Z[5]; E = Z[3]; F = Z[2]; G = Z[1]; H = Z[0];
  //   i3 = In[0]; i2 = In[1]; i1 = In[2]
endmodule
