// Digital circuit Template-04.dig as structural Verilog
module Template_04 (
  input  [6:0] In,
  output [6:0] Output
);

  wire C1, C2, C3;
  wire [6:0] decoder_1_out_1;

  xor xor_1 (C1, In[3], In[2], In[1], In[0]);
  xor xor_2 (C2, In[5], In[4], In[1], In[0]);
  xor xor_3 (C3, In[6], In[4], In[2], In[0]);
  Decoder #(.Selector_Bits(3)) decoder_1 (
    .sel({C1, C2, C3}), .out_1(decoder_1_out_1[6]), .out_2(decoder_1_out_1[5]), .out_3(decoder_1_out_1[4]),
    .out_4(decoder_1_out_1[3]), .out_5(decoder_1_out_1[2]), .out_6(decoder_1_out_1[1]),
    .out_7(decoder_1_out_1[0]));  // open: out_0
  assign Output = decoder_1_out_1 ^ In;  // XOr xor_4, 7 bits wide

  // Other names for the same wires on the sheet: i7 = In[0]; i6 = In[1]; i5 = In[2]; i4 = In[3]; i3 = In[4];
  //   i2 = In[5]; i1 = In[6]
endmodule
