// Digital circuit solution.dig as structural Verilog
module solution (
  input  SM,
  input  SN,
  input  TE,
  input  RA,
  input  AH,
  input  LI,
  input  MW,
  input  MF,
  output WP,
  output FD
);

  wire and_1_out, and_2_out, and_3_out, not_1_out, not_2_out, not_3_out, not_4_out, not_5_out, not_6_out,
       not_7_out, not_8_out, not_9_out, or_1_out, or_3_out;

  not not_1 (not_1_out, SM);
  not not_2 (not_2_out, SN);
  not not_3 (not_3_out, TE);
  not not_4 (not_4_out, RA);
  not not_5 (not_5_out, AH);
  not not_6 (not_6_out, LI);
  not not_7 (not_7_out, MW);
  not not_8 (not_8_out, MF);
  and and_1 (and_1_out, SM, not_4_out, LI);
  or or_1 (or_1_out, TE, AH);
  and and_2 (and_2_out, and_1_out, or_1_out);
  and and_3 (and_3_out, SN, not_1_out, not_4_out);
  or or_2 (WP, MW, and_2_out);
  or or_3 (or_3_out, MF, and_3_out);
  not not_9 (not_9_out, WP);
  and and_4 (FD, not_9_out, or_3_out);

  // Notes on the sheet:
  //   WP: WP – Water Pump (1=เปิดรดน้ำ)
  //   FD: FD – Fertilizer Dispenser (1=เปิดใส่ปุ๋ย)
  //   SM: SM – Soil Moisture (ดินแห้ง=1, ดินชื้น=0)
  //   SN: SN – Soil Nutrient (ธาตุอาหารต่ำ=1, เพียงพอ=0)
  //   TE: TE – Temperature (อุณหภูมิสูงเกิน 35°C =1)
  //   RA: RA – Rain (มีฝนตก=1, ไม่มีฝน=0)
  //   AH: AH – Air Humidity (ความชื้นอากาศต่ำ=1)
  //   LI: LI – Light (แสงแดดแรง=1)
  //   MW: MW – Manual Water (ผู้ใช้สั่ง “รดน้ำ” =1)
  //   MF: MF – Manual Fertilize (ผู้ใช้สั่ง “ใส่ปุ๋ย” =1)
  //   Don't change anything inside this box
endmodule

/* Test case T1:
SM SN TE RA AH LI MW MF        WP FD
0  0  0  0  0  0  0  0         0  0
1  0  1  0  0  1  0  0         1  0
1  0  1  0  0  0  0  0         0  0
0  0  0  0  0  0  1  0         1  0
0  0  0  0  0  0  0  1         0  1
*/
