// Digital circuit solution.dig as structural Verilog
module solution (
  input  reset,
  input  clk,
  output A,
  output B,
  output C
);

  wire [2:0] lookuptable_1_out, multiplexer_1_out;

  LookUpTable #(.Bits(3)) lookuptable_1 (.in0(A), .in1(B), .in2(C), .out(lookuptable_1_out));
  Multiplexer #(.Bits(3)) multiplexer_1 (.sel(reset), .in_0(lookuptable_1_out), .in_1(3'b000), .out(multiplexer_1_out));
  D_FF #(.Bits(3)) d_ff_1 (.D(multiplexer_1_out), .C(clk), .Q({C, B, A}));  // open: nQ

  // Notes on the sheet:
  //   contents of lookuptable_1 (hex, n*v repeats v):
  //   1,b,6e,a,0,64,6f,65
endmodule
