// Digital circuit solution.dig as structural Verilog
module solution (
  input  \input ,
  input  clk,
  input  [15:0] A,
  output busy,
  output [7:0] sqrt
);

  wire _00, _01, _10, _11, and_2_out, comparator_2_eq, d_ff_2_q, finish, gt, load_a_t, multiplexer_1_out,
       multiplexer_2_out, Qa, st;
  wire [0:0] QaQb;
  wire [7:0] a_n_t, add_1_s, multiplexer_3_out, multiplexer_4_out, sub_1_s;
  wire [15:0] a_2, A_n;

  Multiplexer #(.Selector_Bits(2)) multiplexer_1 (
    .sel({Qa, QaQb[0]}), .in_0(1'b0), .in_1(finish), .in_2(1'b0), .in_3(1'b0), .out(multiplexer_1_out));
  D_FF d_ff_1 (.D(multiplexer_1_out), .C(clk), .Q(Qa));  // open: nQ
  D_FF d_ff_2 (.D(\input ), .C(clk), .Q(d_ff_2_q));  // open: nQ
  Register #(.Bits(16)) register_1 (.D(A), .C(clk), .en(_00), .Q(A_n));
  Add #(.Bits(8)) add_1 (.a(a_n_t), .b(8'h1), .c_i(1'b0), .s(add_1_s));  // open: c_o
  Sub #(.Bits(8)) sub_1 (.a(a_n_t), .b(8'h1), .c_i(1'b0), .s(sub_1_s));  // open: c_o
  and and_1 (st, ~d_ff_2_q, \input );  // And
  Multiplexer #(.Selector_Bits(2)) multiplexer_2 (
    .sel({Qa, QaQb[0]}), .in_0(st), .in_1(1'b1), .in_2(1'b1), .in_3(1'b0), .out(multiplexer_2_out));
  D_FF d_ff_3 (.D(multiplexer_2_out), .C(clk), .Q(QaQb[0]));  // open: nQ
  Decoder #(.Selector_Bits(2)) decoder_1 (.sel({Qa, QaQb[0]}), .out_0(_00), .out_1(_01), .out_2(_10), .out_3(_11));
  Multiplexer #(.Bits(8)) multiplexer_3 (.sel(_00), .in_0(add_1_s), .in_1({8{1'b0}}), .out(multiplexer_3_out));
  Multiplexer #(.Bits(8)) multiplexer_4 (.sel(gt), .in_0(a_n_t), .in_1(sub_1_s), .out(multiplexer_4_out));
  Register #(.Bits(8)) register_2 (.D(multiplexer_3_out), .C(clk), .en(load_a_t), .Q(a_n_t));
  Comparator #(.Bits(16)) comparator_1 (.a(a_2), .b(A_n), .gt(gt));  // open: eq, lt
  Mul #(.Bits(8)) mul_1 (.a(a_n_t), .b(a_n_t), .mul(a_2));
  Register #(.Bits(8)) register_3 (.D(multiplexer_4_out), .C(clk), .en(_11), .Q(sqrt));
  and and_2 (and_2_out, _01, ~finish);  // And
  Comparator #(.Bits(8)) comparator_2 (.a(a_n_t), .b({8{1'b1}}), .eq(comparator_2_eq));  // open: gt, lt
  or or_1 (load_a_t, and_2_out, _00);
  or or_2 (finish, gt, comparator_2_eq);
  not not_1 (busy, _00);

  // Other names for the same wires on the sheet: in = \input ; load_A = _00; load_out = _11; QaQb[1] = Qa;
  //   Qb = QaQb[0]
endmodule

/* Test case Test 3:
clk A input sqrt busy
0 0 0 0 0
1 0 0 0 0
0 0 0 0 0
1 0 0 0 0
0 65026 1 X X
1 65026 1 X X
loop(x,1000)
0 65026 0 X X
1 65026 0 X X
end loop
0 0 0 255 0
1 0 0 255 0
*/

/* Test case Test 2:
clk A input sqrt busy
0 0 0 0 0
1 0 0 0 0
0 0 0 0 0
1 0 0 0 0
0 1 1 X X
1 1 1 X X
loop(x,1000)
0 1 0 X X
1 1 0 X X
end loop
0 0 0 1 0
1 0 0 1 0
*/

/* Test case Test 1:
clk A input sqrt busy
0 0 0 0 0
1 0 0 0 0
0 0 0 0 0
1 0 0 0 0
0 0 1 X X
1 0 1 X X
loop(x,1000)
0 0 0 X X
1 0 0 X X
end loop
0 0 0 0 0
1 0 0 0 0
*/
