// Digital circuit solution.dig as structural Verilog
module solution (
  input  \input ,
  input  clk,
  input  [15:0] A,
  input  reset,
  output busy,
  output [15:0] mean,
  output [31:0] out_7,
  output [31:0] out_8,
  output [31:0] out_9,
  output [31:0] out_10,
  output [15:0] out_11,
  output [31:0] out_12
);

  wire and_1_out, d_ff_1_q, multiplexer_1_out, run;
  wire [15:0] multiplexer_6_out, multiplexer_7_out;
  wire [31:0] add_2_s, div_1_q, multiplexer_2_out, multiplexer_3_out, multiplexer_4_out;

  Add #(.Bits(32)) add_1 (.a(out_7), .b(32'h1), .c_i(1'b0), .s(out_12));  // open: c_o
  Multiplexer multiplexer_1 (.sel(reset), .in_0(\input ), .in_1(1'b0), .out(multiplexer_1_out));
  D_FF d_ff_1 (.D(multiplexer_1_out), .C(clk), .Q(d_ff_1_q));  // open: nQ
  Add #(.Bits(32)) add_2 (.a(multiplexer_4_out), .b(out_9), .c_i(1'b0), .s(add_2_s));  // open: c_o
  Div #(.Bits(32)) div_1 (.a(out_10), .b(out_12), .q(div_1_q));  // open: r
  Multiplexer #(.Bits(32)) multiplexer_2 (.sel(run), .in_0(out_8), .in_1({{16{1'b0}}, A}), .out(multiplexer_2_out));
  Counter #(.Bits(32)) counter_1 (.en(run), .C(clk), .clr(reset), .out(out_7));  // open: ovf
  Multiplexer #(.Bits(32)) multiplexer_3 (.sel(run), .in_0(out_9), .in_1(add_2_s), .out(multiplexer_3_out));
  and and_1 (and_1_out, ~d_ff_1_q, \input );  // And
  Multiplexer #(.Bits(32)) multiplexer_4 (
    .sel(reset), .in_0(multiplexer_2_out), .in_1({32{1'b0}}), .out(multiplexer_4_out));
  Multiplexer #(.Bits(32)) multiplexer_5 (.sel(reset), .in_0(multiplexer_3_out), .in_1({32{1'b0}}), .out(out_10));
  Multiplexer #(.Bits(16)) multiplexer_6 (.sel(run), .in_0(mean), .in_1(div_1_q[15:0]), .out(multiplexer_6_out));
  and and_2 (run, ~busy, and_1_out);  // And
  D_FF #(.Bits(32)) d_ff_2 (.D(multiplexer_4_out), .C(clk), .Q(out_8));  // open: nQ
  D_FF #(.Bits(32)) d_ff_3 (.D(out_10), .C(clk), .Q(out_9));  // open: nQ
  Multiplexer #(.Bits(16)) multiplexer_7 (
    .sel(reset), .in_0(multiplexer_6_out), .in_1({16{1'b0}}), .out(multiplexer_7_out));
  D_FF #(.Bits(16)) d_ff_4 (.D(multiplexer_7_out), .C(clk), .Q(mean));  // open: nQ
  D_FF d_ff_5 (.D(run), .C(clk), .Q(busy));  // open: nQ

  assign out_11 = mean;

  // Other names for the same wires on the sheet: A_t[15:0] = A; in = \input ; N[31:0] = out_7; r = reset;
  //   sum[31:0] = out_9; X[31:0] = out_8
endmodule

/* Test case Test 3:
clk A input reset mean busy
0 0 0 0 0 0
1 0 0 0 0 0
0 0 0 1 0 0
1 0 0 1 0 0
0 0 0 0 0 0
1 0 0 0 0 0
0 65535 1 0 X X
1 65535 1 0 X X
0 65535 0 0 X X
1 65535 0 0 X X
loop(x,500)
end loop
0 0 0 0 65535 0
1 0 0 0 65535 0
0 65535 1 0 X X
1 65535 1 0 X X
0 65535 0 0 X X
1 65535 0 0 X X
loop(x,500)
end loop
0 0 0 0 65535 0
1 0 0 0 65535 0
*/

/* Test case Test 2:
clk A input reset mean busy
0 0 0 0 0 0
1 0 0 0 0 0
0 0 0 1 0 0
1 0 0 1 0 0
0 0 0 0 0 0
1 0 0 0 0 0
0 5 1 0 X X
1 5 1 0 X X
0 5 0 0 X X
1 5 0 0 X X
loop(x,500)
end loop
0 0 0 0 5 0
1 0 0 0 5 0
0 15 1 0 X X
1 15 1 0 X X
0 15 0 0 X X
1 15 0 0 X X
loop(x,500)
end loop
0 0 0 0 10 0
1 0 0 0 10 0
*/

/* Test case Test 1:
clk A input reset mean busy
0 0 0 0 0 0
1 0 0 0 0 0
0 0 0 1 0 0
1 0 0 1 0 0
0 0 0 0 0 0
1 0 0 0 0 0
0 5 1 0 X X
1 5 1 0 X X
0 5 0 0 X X
1 5 0 0 X X
loop(x,500)
end loop
0 0 0 0 5 0
1 0 0 0 5 0
*/
