// Digital circuit solution.dig as structural Verilog
module solution (
  input  reset,
  input  [7:0] N,
  input  \new ,
  input  clock,
  output [7:0] num_inc,
  output [7:0] max,
  output busy
);

  wire and_1_out, and_2_out, comparator_1_gt, d_ff_1_q, multiplexer_1_out, run;
  wire [7:0] multiplexer_2_out, multiplexer_3_out, multiplexer_4_out;

  Multiplexer multiplexer_1 (.sel(reset), .in_0(\new ), .in_1(1'b0), .out(multiplexer_1_out));
  Comparator #(.Bits(8)) comparator_1 (.a(N), .b(max), .gt(comparator_1_gt));  // open: eq, lt
  D_FF d_ff_1 (.D(multiplexer_1_out), .C(clock), .Q(d_ff_1_q));  // open: nQ
  and and_1 (and_1_out, comparator_1_gt, run);
  and and_2 (and_2_out, ~d_ff_1_q, \new );  // And
  Counter #(.Bits(8)) counter_1 (.en(and_1_out), .C(clock), .clr(reset), .out(num_inc));  // open: ovf
  Multiplexer #(.Bits(8)) multiplexer_2 (.sel(comparator_1_gt), .in_0(max), .in_1(N), .out(multiplexer_2_out));
  and and_3 (run, ~busy, and_2_out);  // And
  Multiplexer #(.Bits(8)) multiplexer_3 (.sel(run), .in_0(max), .in_1(multiplexer_2_out), .out(multiplexer_3_out));
  D_FF d_ff_2 (.D(run), .C(clock), .Q(busy));  // open: nQ
  Multiplexer #(.Bits(8)) multiplexer_4 (
    .sel(reset), .in_0(multiplexer_3_out), .in_1({8{1'b0}}), .out(multiplexer_4_out));
  D_FF #(.Bits(8)) d_ff_3 (.D(multiplexer_4_out), .C(clock), .Q(max));  // open: nQ

  // Other names for the same wires on the sheet: busy_m = busy; clk = clock; max_m[7:0] = max; num_m[7:0] = num_inc;
  //   R = reset
endmodule

/* Test case T06:
N new reset clock num_inc max busy
0 0 1 0 x x x
0 0 1 1 0 0 0
131 1 0 0 x x x
131 1 0 1 x x x
0 0 0 0 x x x
0 0 0 1 x x x
0 0 0 0 x x x
0 0 0 1 x x x
0 0 0 0 x x x
0 0 0 1 x x x
0 0 0 0 x x x
0 0 0 1 x x x
0 0 0 0 x x x
0 0 0 1 x x x
0 0 0 0 x x x
0 0 0 1 x x x
0 0 0 0 x x x
0 0 0 1 x x x
0 0 0 0 x x x
0 0 0 1 x x x
0 0 0 0 x x x
0 0 0 1 x x x
0 0 0 0 x x x
0 0 0 1 x x x
0 0 0 0 x x x
0 0 0 1 x x x
0 0 0 0 x x x
0 0 0 1 x x x
0 0 0 0 x x x
0 0 0 1 x x x
0 0 0 0 x x x
0 0 0 1 x x x
0 0 0 0 x x x
0 0 0 1 x x x
0 0 0 0 x x x
0 0 0 1 x x x
0 0 0 0 x x x
0 0 0 1 x x x
0 0 0 0 x x x
0 0 0 1 x x x
0 0 0 0 x x x
0 0 0 1 x x x
0 0 0 0 x x x
0 0 0 1 x x x
0 0 0 0 x x x
0 0 0 1 x x x
0 0 0 0 x x x
0 0 0 1 x x x
0 0 0 0 x x x
0 0 0 1 x x x
0 0 0 0 x x x
0 0 0 1 x x x
0 0 0 0 x x x
0 0 0 1 x x x
0 0 0 0 x x x
0 0 0 1 x x x
0 0 0 0 x x x
0 0 0 1 x x x
0 0 0 0 x x x
0 0 0 1 x x x
0 0 0 0 x x x
0 0 0 1 x x x
0 0 0 0 x x x
0 0 0 1 x x x
0 0 0 0 1 131 0
0 0 0 1 1 131 0
130 1 0 0 x x x
130 1 0 1 x x x
0 0 0 0 x x x
0 0 0 1 x x x
0 0 0 0 x x x
0 0 0 1 x x x
0 0 0 0 x x x
0 0 0 1 x x x
0 0 0 0 x x x
0 0 0 1 x x x
0 0 0 0 x x x
0 0 0 1 x x x
0 0 0 0 x x x
0 0 0 1 x x x
0 0 0 0 x x x
0 0 0 1 x x x
0 0 0 0 x x x
0 0 0 1 x x x
0 0 0 0 x x x
0 0 0 1 x x x
0 0 0 0 x x x
0 0 0 1 x x x
0 0 0 0 x x x
0 0 0 1 x x x
0 0 0 0 x x x
0 0 0 1 x x x
0 0 0 0 x x x
0 0 0 1 x x x
0 0 0 0 x x x
0 0 0 1 x x x
0 0 0 0 x x x
0 0 0 1 x x x
0 0 0 0 x x x
0 0 0 1 x x x
0 0 0 0 x x x
0 0 0 1 x x x
0 0 0 0 x x x
0 0 0 1 x x x
0 0 0 0 x x x
0 0 0 1 x x x
0 0 0 0 x x x
0 0 0 1 x x x
0 0 0 0 x x x
0 0 0 1 x x x
0 0 0 0 x x x
0 0 0 1 x x x
0 0 0 0 x x x
0 0 0 1 x x x
0 0 0 0 x x x
0 0 0 1 x x x
0 0 0 0 x x x
0 0 0 1 x x x
0 0 0 0 x x x
0 0 0 1 x x x
0 0 0 0 x x x
0 0 0 1 x x x
0 0 0 0 x x x
0 0 0 1 x x x
0 0 0 0 x x x
0 0 0 1 x x x
0 0 0 0 x x x
0 0 0 1 x x x
0 0 0 0 1 131 0
0 0 0 1 1 131 0
58 1 0 0 x x x
58 1 0 1 x x x
0 0 0 0 x x x
0 0 0 1 x x x
0 0 0 0 x x x
0 0 0 1 x x x
0 0 0 0 x x x
0 0 0 1 x x x
0 0 0 0 x x x
0 0 0 1 x x x
0 0 0 0 x x x
0 0 0 1 x x x
0 0 0 0 x x x
0 0 0 1 x x x
0 0 0 0 x x x
0 0 0 1 x x x
0 0 0 0 x x x
0 0 0 1 x x x
0 0 0 0 x x x
0 0 0 1 x x x
0 0 0 0 x x x
0 0 0 1 x x x
0 0 0 0 x x x
0 0 0 1 x x x
0 0 0 0 x x x
0 0 0 1 x x x
0 0 0 0 x x x
0 0 0 1 x x x
0 0 0 0 x x x
0 0 0 1 x x x
0 0 0 0 x x x
0 0 0 1 x x x
0 0 0 0 x x x
0 0 0 1 x x x
0 0 0 0 x x x
0 0 0 1 x x x
0 0 0 0 x x x
0 0 0 1 x x x
0 0 0 0 x x x
0 0 0 1 x x x
0 0 0 0 x x x
0 0 0 1 x x x
0 0 0 0 x x x
0 0 0 1 x x x
0 0 0 0 x x x
0 0 0 1 x x x
0 0 0 0 x x x
0 0 0 1 x x x
0 0 0 0 x x x
0 0 0 1 x x x
0 0 0 0 x x x
0 0 0 1 x x x
0 0 0 0 x x x
0 0 0 1 x x x
0 0 0 0 x x x
0 0 0 1 x x x
0 0 0 0 x x x
0 0 0 1 x x x
0 0 0 0 x x x
0 0 0 1 x x x
0 0 0 0 x x x
0 0 0 1 x x x
0 0 0 0 1 131 0
0 0 0 1 1 131 0
154 1 0 0 x x x
154 1 0 1 x x x
0 0 0 0 x x x
0 0 0 1 x x x
0 0 0 0 x x x
0 0 0 1 x x x
0 0 0 0 x x x
0 0 0 1 x x x
0 0 0 0 x x x
0 0 0 1 x x x
0 0 0 0 x x x
0 0 0 1 x x x
0 0 0 0 x x x
0 0 0 1 x x x
0 0 0 0 x x x
0 0 0 1 x x x
0 0 0 0 x x x
0 0 0 1 x x x
0 0 0 0 x x x
0 0 0 1 x x x
0 0 0 0 x x x
0 0 0 1 x x x
0 0 0 0 x x x
0 0 0 1 x x x
0 0 0 0 x x x
0 0 0 1 x x x
0 0 0 0 x x x
0 0 0 1 x x x
0 0 0 0 x x x
0 0 0 1 x x x
0 0 0 0 x x x
0 0 0 1 x x x
0 0 0 0 x x x
0 0 0 1 x x x
0 0 0 0 x x x
0 0 0 1 x x x
0 0 0 0 x x x
0 0 0 1 x x x
0 0 0 0 x x x
0 0 0 1 x x x
0 0 0 0 x x x
0 0 0 1 x x x
0 0 0 0 x x x
0 0 0 1 x x x
0 0 0 0 x x x
0 0 0 1 x x x
0 0 0 0 x x x
0 0 0 1 x x x
0 0 0 0 x x x
0 0 0 1 x x x
0 0 0 0 x x x
0 0 0 1 x x x
0 0 0 0 x x x
0 0 0 1 x x x
0 0 0 0 x x x
0 0 0 1 x x x
0 0 0 0 x x x
0 0 0 1 x x x
0 0 0 0 x x x
0 0 0 1 x x x
0 0 0 0 x x x
0 0 0 1 x x x
0 0 0 0 2 154 0
0 0 0 1 2 154 0
122 1 0 0 x x x
122 1 0 1 x x x
0 0 0 0 x x x
0 0 0 1 x x x
0 0 0 0 x x x
0 0 0 1 x x x
0 0 0 0 x x x
0 0 0 1 x x x
0 0 0 0 x x x
0 0 0 1 x x x
0 0 0 0 x x x
0 0 0 1 x x x
0 0 0 0 x x x
0 0 0 1 x x x
0 0 0 0 x x x
0 0 0 1 x x x
0 0 0 0 x x x
0 0 0 1 x x x
0 0 0 0 x x x
0 0 0 1 x x x
0 0 0 0 x x x
0 0 0 1 x x x
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*/
