// Digital circuit solve_no_loop.dig as structural Verilog
module solve_no_loop (
  input  reset,
  input  [7:0] M,
  input  start,
  input  clock,
  input  [7:0] N,
  output [15:0] Z,
  output busy
);

  wire and_1_out, comparator_1_lt, d_ff_1_q, multiplexer_1_out, run;
  wire [7:0] a, add_1_s, add_2_s, div_1_r, div_2_r, div_3_q, l, n_t, sub_1_s, sub_2_s;
  wire [15:0] div_4_q, mul_1_mul, multiplexer_4_out, multiplexer_5_out, multiplexer_6_out;

  Multiplexer multiplexer_1 (.sel(reset), .in_0(start), .in_1(1'b0), .out(multiplexer_1_out));
  Div #(.Bits(8)) div_1 (.a(M), .b(8'h2), .r(div_1_r));  // open: q
  Div #(.Bits(8)) div_2 (.a(N), .b(8'h2), .r(div_2_r));  // open: q
  D_FF d_ff_1 (.D(multiplexer_1_out), .C(clock), .Q(d_ff_1_q));  // open: nQ
  Add #(.Bits(8)) add_1 (.a(M), .b(8'h1), .c_i(1'b0), .s(add_1_s));  // open: c_o
  Sub #(.Bits(8)) sub_1 (.a(N), .b(8'h1), .c_i(1'b0), .s(sub_1_s));  // open: c_o
  and and_1 (and_1_out, ~d_ff_1_q, start);  // And
  Multiplexer #(.Bits(8)) multiplexer_2 (.sel(div_1_r[0]), .in_0(M), .in_1(add_1_s), .out(a));
  Multiplexer #(.Bits(8)) multiplexer_3 (.sel(div_2_r[0]), .in_0(N), .in_1(sub_1_s), .out(l));
  and and_2 (run, ~busy, and_1_out);  // And
  Sub #(.Bits(8)) sub_2 (.a(N), .b(M), .c_i(1'b0), .s(sub_2_s));  // open: c_o
  Add #(.Bits(8)) add_2 (.a(a), .b(l), .c_i(1'b0), .s(add_2_s));  // open: c_o
  Div #(.Bits(8)) div_3 (.a(sub_2_s), .b(8'h2), .q(div_3_q));  // open: r
  Mul #(.Bits(8)) mul_1 (.a(add_2_s), .b(n_t), .mul(mul_1_mul));
  D_FF d_ff_2 (.D(run), .C(clock), .Q(busy));  // open: nQ
  Add #(.Bits(8)) add_3 (.a(div_3_q), .b(8'h1), .c_i(1'b0), .s(n_t));  // open: c_o
  Comparator #(.Bits(8)) comparator_1 (.a(M), .b(N), .lt(comparator_1_lt));  // open: gt, eq
  Div #(.Bits(16)) div_4 (.a(mul_1_mul), .b(16'h2), .q(div_4_q));  // open: r
  Multiplexer #(.Bits(16)) multiplexer_4 (
    .sel(comparator_1_lt), .in_0({16{1'b0}}), .in_1(div_4_q), .out(multiplexer_4_out));
  Multiplexer #(.Bits(16)) multiplexer_5 (.sel(run), .in_0(Z), .in_1(multiplexer_4_out), .out(multiplexer_5_out));
  Multiplexer #(.Bits(16)) multiplexer_6 (
    .sel(reset), .in_0(multiplexer_5_out), .in_1({16{1'b0}}), .out(multiplexer_6_out));
  D_FF #(.Bits(16)) d_ff_3 (.D(multiplexer_6_out), .C(clock), .Q(Z));  // open: nQ

  // Other names for the same wires on the sheet: clk = clock; R = reset; S = start; Z_m[15:0] = Z
endmodule

/* Test case T01:
 M  N start clock reset Z busy
 0  0 0     0     1     x x
 0  0 0     1     1     x 0
 0  0 0     0     1     x 0
 0  0 0     1     1     x 0
 1 10 1     0     0     x 0
 1 10 1     1     0     x 1
 0  0 0     0     0     x 1
 0  0 0     1     0     x 1
 0  0 0     0     0     x 1
 0  0 0     1     0     x 1
 0  0 0     0     0     x 1
 0  0 0     1     0     x x
 0  0 0     0     0     x x
 0  0 0     1     0     x x
 0  0 0     0     0     x x
 0  0 0     1     0     x x
 0  0 0     0     0     x x
 0  0 0     1     0     x x
 0  0 0     0     0     x x
 0  0 0     1     0     x x
 0  0 0     0     0     x x
 0  0 0     1     0     x x
 0  0 0     0     0     x x
 0  0 0     1     0     x x
 0  0 0     0     0     x x
 0  0 0     1     0     x x
 0  0 0     0     0     x x
 0  0 0     1     0     x x
 0  0 0     0     0     x x
 0  0 0     1     0     x x
 0  0 0     0     0     x x
 0  0 0     1     0     x x
 0  0 0     0     0     x x
 0  0 0     1     0     x x
 0  0 0     0     0     x x
 0  0 0     1     0     x x
 0  0 0     0     0     x x
 0  0 0     1     0     x x
 0  0 0     0     0     x x
 0  0 0     1     0     x x
 0  0 0     0     0     x x
 0  0 0     1     0     x x
 0  0 0     0     0     x x
 0  0 0     1     0     x x
 0  0 0     0     0     x x
 0  0 0     1     0     x x
 0  0 0     0     0     x x
 0  0 0     1     0     x x
 0  0 0     0     0     x x
 0  0 0     1     0     x x
 0  0 0     0     0     x x
 0  0 0     1     0     x x
 0  0 0     0     0     x x
 0  0 0     1     0     x x
 0  0 0     0     0     x x
 0  0 0     1     0     x x
 0  0 0     0     0     x x
 0  0 0     1     0     x x
 0  0 0     0     0     x x
 0  0 0     1     0     x x
 0  0 0     0     0     x x
 0  0 0     1     0     x x
 0  0 0     0     0     x x
 0  0 0     1     0     x x
 0  0 0     0     0     x x
 0  0 0     1     0     x x
 0  0 0     0     0     x x
 0  0 0     1     0     x x
 0  0 0     0     0     x x
 0  0 0     1     0     x x
 0  0 0     0     0     x x
 0  0 0     1     0     x x
 0  0 0     0     0     x x
 0  0 0     1     0     x x
 0  0 0     0     0     x x
 0  0 0     1     0     x x
 0  0 0     0     0     x x
 0  0 0     1     0     x x
 0  0 0     0     0     x x
 0  0 0     1     0     x x
 0  0 0     0     0     x x
 0  0 0     1     0     x x
 0  0 0     0     0     x x
 0  0 0     1     0     x x
 0  0 0     0     0     x x
 0  0 0     1     0     x x
 0  0 0     0     0     x x
 0  0 0     1     0     x x
 0  0 0     0     0     x x
 0  0 0     1     0     x x
 0  0 0     0     0     x x
 0  0 0     1     0     x x
 0  0 0     0     0     x x
 0  0 0     1     0     x x
 0  0 0     0     0     x x
 0  0 0     1     0     x x
 0  0 0     0     0     x x
 0  0 0     1     0     x x
 0  0 0     0     0     x x
 0  0 0     1     0     x x
 0  0 0     0     0     x x
 0  0 0     1     0     x x
 0  0 0     0     0     x x
 0  0 0     1     0     x x
 0  0 0     0     0     x x
 0  0 0     1     0     x x
 0  0 0     0     0     x x
 0  0 0     1     0     x x
 0  0 0     0     0     x x
 0  0 0     1     0     x x
 0  0 0     0     0     x x
 0  0 0     1     0     x x
 0  0 0     0     0     x x
 0  0 0     1     0     x x
 0  0 0     0     0     30 0
 0  0 0     1     0     30 0
 0  0 0     0     0     30 0
 0  0 0     1     0     30 0
*/
