// Digital circuit solution.dig as structural Verilog
module solution (
  input  reset,
  input  [7:0] M,
  input  start,
  input  clock,
  input  [7:0] N,
  output [15:0] Z,
  output busy
);

  wire _00, _01, _10, _11, comparator_1_lt, d_ff_2_q, gt, load_m, load_out, load_z, multiplexer_1_out,
       multiplexer_2_out, multiplexer_3_out, multiplexer_4_out, multiplexer_6_out, Qa, st;
  wire [0:0] QaQb;
  wire [15:0] add_1_s, add_2_s, add_3_s, M_n, multiplexer_5_out, multiplexer_7_out, multiplexer_8_out,
       multiplexer_9_out, N_n, Z_n;

  Multiplexer #(.Selector_Bits(2)) multiplexer_1 (
    .sel({Qa, QaQb[0]}), .in_0(1'b0), .in_1(gt), .in_2(1'b1), .in_3(1'b0), .out(multiplexer_1_out));
  Multiplexer multiplexer_2 (.sel(reset), .in_0(multiplexer_1_out), .in_1(1'b0), .out(multiplexer_2_out));
  D_FF d_ff_1 (.D(multiplexer_2_out), .C(clock), .Q(Qa));  // open: nQ
  Add #(.Bits(16)) add_1 (.a(M_n), .b({16{1'b0}}), .c_i(M_n[0]), .s(add_1_s));  // open: c_o
  Decoder #(.Selector_Bits(2)) decoder_1 (.sel({Qa, QaQb[0]}), .out_0(_00), .out_1(_01), .out_2(_10), .out_3(_11));
  Multiplexer multiplexer_3 (.sel(reset), .in_0(start), .in_1(1'b0), .out(multiplexer_3_out));
  Comparator #(.Bits(16)) comparator_1 (.a(N_n), .b(M_n), .lt(comparator_1_lt));  // open: gt, eq
  Multiplexer #(.Selector_Bits(2)) multiplexer_4 (
    .sel({Qa, QaQb[0]}), .in_0(st), .in_1(1'b0), .in_2(1'b1), .in_3(1'b1), .out(multiplexer_4_out));
  D_FF d_ff_2 (.D(multiplexer_3_out), .C(clock), .Q(d_ff_2_q));  // open: nQ
  not not_1 (gt, comparator_1_lt);
  Multiplexer #(.Bits(16)) multiplexer_5 (.sel(_00), .in_0(add_1_s), .in_1({{8{1'b0}}, M}), .out(multiplexer_5_out));
  Add #(.Bits(16)) add_2 (.a(M_n), .b(Z_n), .c_i(1'b0), .s(add_2_s));  // open: c_o
  Multiplexer multiplexer_6 (.sel(reset), .in_0(multiplexer_4_out), .in_1(1'b0), .out(multiplexer_6_out));
  and and_1 (st, ~d_ff_2_q, start);  // And
  Add #(.Bits(16)) add_3 (.a(M_n), .b(16'h2), .c_i(1'b0), .s(add_3_s));  // open: c_o
  Multiplexer #(.Bits(16)) multiplexer_7 (.sel(reset), .in_0(Z_n), .in_1({16{1'b0}}), .out(multiplexer_7_out));
  D_FF d_ff_3 (.D(multiplexer_6_out), .C(clock), .Q(QaQb[0]));  // open: nQ
  Register #(.Bits(16)) register_1 (.D({{8{1'b0}}, N}), .C(clock), .en(_00), .Q(N_n));
  Multiplexer #(.Bits(16)) multiplexer_8 (.sel(_11), .in_0(multiplexer_5_out), .in_1(add_3_s), .out(multiplexer_8_out));
  Multiplexer #(.Bits(16)) multiplexer_9 (.sel(reset), .in_0(add_2_s), .in_1({16{1'b0}}), .out(multiplexer_9_out));
  Register #(.Bits(16)) register_2 (.D(multiplexer_9_out), .C(clock), .en(load_z), .Q(Z_n));
  Register #(.Bits(16)) register_3 (.D(multiplexer_7_out), .C(clock), .en(load_out), .Q(Z));
  Register #(.Bits(16)) register_4 (.D(multiplexer_8_out), .C(clock), .en(load_m), .Q(M_n));
  not not_2 (busy, _00);
  or or_1 (load_m, _00, _01, _11);
  or or_2 (load_z, _10, reset);
  or or_3 (load_out, _00, reset);

  // Other names for the same wires on the sheet: clk = clock; load_n = _00; M_t[7:0] = M; N_t[7:0] = N;
  //   Out_n[15:0] = Z; QaQb[1] = Qa; Qb = QaQb[0]; R = reset; S = start

  // Notes on the sheet:
  //   state logic
  //   data path
  //   control
endmodule

/* Test case T01:
 M  N start clock reset Z busy
 0  0 0     0     1     x x
 0  0 0     1     1     x 0
 0  0 0     0     1     x 0
 0  0 0     1     1     x 0
 1 10 1     0     0     x 0
 1 10 1     1     0     x 1
 0  0 0     0     0     x 1
 0  0 0     1     0     x 1
 0  0 0     0     0     x 1
 0  0 0     1     0     x 1
 0  0 0     0     0     x 1
 0  0 0     1     0     x x
 0  0 0     0     0     x x
 0  0 0     1     0     x x
 0  0 0     0     0     x x
 0  0 0     1     0     x x
 0  0 0     0     0     x x
 0  0 0     1     0     x x
 0  0 0     0     0     x x
 0  0 0     1     0     x x
 0  0 0     0     0     x x
 0  0 0     1     0     x x
 0  0 0     0     0     x x
 0  0 0     1     0     x x
 0  0 0     0     0     x x
 0  0 0     1     0     x x
 0  0 0     0     0     x x
 0  0 0     1     0     x x
 0  0 0     0     0     x x
 0  0 0     1     0     x x
 0  0 0     0     0     x x
 0  0 0     1     0     x x
 0  0 0     0     0     x x
 0  0 0     1     0     x x
 0  0 0     0     0     x x
 0  0 0     1     0     x x
 0  0 0     0     0     x x
 0  0 0     1     0     x x
 0  0 0     0     0     x x
 0  0 0     1     0     x x
 0  0 0     0     0     x x
 0  0 0     1     0     x x
 0  0 0     0     0     x x
 0  0 0     1     0     x x
 0  0 0     0     0     x x
 0  0 0     1     0     x x
 0  0 0     0     0     x x
 0  0 0     1     0     x x
 0  0 0     0     0     x x
 0  0 0     1     0     x x
 0  0 0     0     0     x x
 0  0 0     1     0     x x
 0  0 0     0     0     x x
 0  0 0     1     0     x x
 0  0 0     0     0     x x
 0  0 0     1     0     x x
 0  0 0     0     0     x x
 0  0 0     1     0     x x
 0  0 0     0     0     x x
 0  0 0     1     0     x x
 0  0 0     0     0     x x
 0  0 0     1     0     x x
 0  0 0     0     0     x x
 0  0 0     1     0     x x
 0  0 0     0     0     x x
 0  0 0     1     0     x x
 0  0 0     0     0     x x
 0  0 0     1     0     x x
 0  0 0     0     0     x x
 0  0 0     1     0     x x
 0  0 0     0     0     x x
 0  0 0     1     0     x x
 0  0 0     0     0     x x
 0  0 0     1     0     x x
 0  0 0     0     0     x x
 0  0 0     1     0     x x
 0  0 0     0     0     x x
 0  0 0     1     0     x x
 0  0 0     0     0     x x
 0  0 0     1     0     x x
 0  0 0     0     0     x x
 0  0 0     1     0     x x
 0  0 0     0     0     x x
 0  0 0     1     0     x x
 0  0 0     0     0     x x
 0  0 0     1     0     x x
 0  0 0     0     0     x x
 0  0 0     1     0     x x
 0  0 0     0     0     x x
 0  0 0     1     0     x x
 0  0 0     0     0     x x
 0  0 0     1     0     x x
 0  0 0     0     0     x x
 0  0 0     1     0     x x
 0  0 0     0     0     x x
 0  0 0     1     0     x x
 0  0 0     0     0     x x
 0  0 0     1     0     x x
 0  0 0     0     0     x x
 0  0 0     1     0     x x
 0  0 0     0     0     x x
 0  0 0     1     0     x x
 0  0 0     0     0     x x
 0  0 0     1     0     x x
 0  0 0     0     0     x x
 0  0 0     1     0     x x
 0  0 0     0     0     x x
 0  0 0     1     0     x x
 0  0 0     0     0     x x
 0  0 0     1     0     x x
 0  0 0     0     0     x x
 0  0 0     1     0     x x
 0  0 0     0     0     x x
 0  0 0     1     0     x x
 0  0 0     0     0     30 0
 0  0 0     1     0     30 0
 0  0 0     0     0     30 0
 0  0 0     1     0     30 0
*/
