// Digital circuit solution.dig as structural Verilog
module solution (
  input  reset,
  input  [3:0] N,
  input  \new ,
  input  clock,
  output [7:0] num3,
  output [7:0] num5,
  output busy
);

  wire and_1_out, and_2_out, and_3_out, comparator_1_eq, comparator_2_eq, d_ff_2_q, multiplexer_2_out,
       multiplexer_3_out, run;
  wire [3:0] div_1_r, div_2_r, multiplexer_1_out, N_s;

  Div #(.Bits(4)) div_1 (.a(N_s), .b(4'b0101), .r(div_1_r));  // open: q
  Div #(.Bits(4)) div_2 (.a(N_s), .b(4'b0011), .r(div_2_r));  // open: q
  Multiplexer #(.Bits(4)) multiplexer_1 (.sel(run), .in_0(N_s), .in_1(N), .out(multiplexer_1_out));
  Multiplexer multiplexer_2 (.sel(reset), .in_0(\new ), .in_1(1'b0), .out(multiplexer_2_out));
  Comparator #(.Bits(4)) comparator_1 (.a(div_1_r), .b(4'b0000), .eq(comparator_1_eq));  // open: gt, lt
  Comparator #(.Bits(4)) comparator_2 (.a(div_2_r), .b(4'b0000), .eq(comparator_2_eq));  // open: gt, lt
  D_FF #(.Bits(4)) d_ff_1 (.D(multiplexer_1_out), .C(clock), .Q(N_s));  // open: nQ
  D_FF d_ff_2 (.D(multiplexer_2_out), .C(clock), .Q(d_ff_2_q));  // open: nQ
  and and_1 (and_1_out, busy, comparator_1_eq);
  and and_2 (and_2_out, busy, comparator_2_eq);
  and and_3 (and_3_out, ~d_ff_2_q, \new );  // And
  and and_4 (run, ~busy, and_3_out);  // And
  Counter #(.Bits(8)) counter_1 (.en(and_1_out), .C(clock), .clr(reset), .out(num5));  // open: ovf
  Counter #(.Bits(8)) counter_2 (.en(and_2_out), .C(clock), .clr(reset), .out(num3));  // open: ovf
  Multiplexer multiplexer_3 (.sel(reset), .in_0(run), .in_1(1'b0), .out(multiplexer_3_out));
  D_FF d_ff_3 (.D(multiplexer_3_out), .C(clock), .Q(busy));  // open: nQ

  // Other names for the same wires on the sheet: clk = clock; m3[7:0] = num3; m5[7:0] = num5; R = reset
endmodule

/* Test case T01:
 N new reset clock num3 num5 busy
 0 0   1     0     x    x    x
 0 0   1     1     x    x    x
14 1   0     0     0    0    x
14 1   0     1     0    0    1
 0 0   0     0     x    x    1
 0 0   0     1     x    x    x
 0 0   0     0     x    x    x
 0 0   0     1     x    x    x
 0 0   0     0     x    x    x
 0 0   0     1     x    x    x
 0 0   0     0     x    x    x
 0 0   0     1     x    x    x
 0 0   0     0     x    x    x
 0 0   0     1     x    x    x
 0 0   0     0     x    x    x
 0 0   0     1     x    x    x
 0 0   0     0     x    x    x
 0 0   0     1     x    x    x
 0 0   0     0     x    x    x
 0 0   0     1     x    x    x
 0 0   0     0     x    x    x
 0 0   0     1     x    x    x
 0 0   0     0     x    x    x
 0 0   0     1     x    x    x
 0 0   0     0     0    0    0
 0 0   0     1     0    0    0
15 1   0     0     0    0    x
15 1   0     1     0    0    1
 0 0   0     0     x    x    1
 0 0   0     1     x    x    x
 0 0   0     0     x    x    x
 0 0   0     1     x    x    x
 0 0   0     0     x    x    x
 0 0   0     1     x    x    x
 0 0   0     0     x    x    x
 0 0   0     1     x    x    x
 0 0   0     0     x    x    x
 0 0   0     1     x    x    x
 0 0   0     0     x    x    x
 0 0   0     1     x    x    x
 0 0   0     0     x    x    x
 0 0   0     1     x    x    x
 0 0   0     0     x    x    x
 0 0   0     1     x    x    x
 0 0   0     0     x    x    x
 0 0   0     1     x    x    x
 0 0   0     0     x    x    x
 0 0   0     1     x    x    x
 0 0   0     0     1    1    0
 0 0   0     1     1    1    0
*/
