// Digital circuit solution.dig as structural Verilog
module solution (
  input  A,
  input  B,
  input  Cin,
  output out_4,
  output out_5
);

  wire _7400_1_pin3, _7400_1_pin6, _7400_1_pin8, _7400_1_pin11, _7400_2_pin3, _7400_2_pin6, _7400_2_pin8;

  _7400 _7400_1 (
    .pin1(A), .pin2(B), .pin3(_7400_1_pin3), .pin4(A), .pin5(_7400_1_pin3), .pin6(_7400_1_pin6), .pin7(1'b0),
    .pin8(_7400_1_pin8), .pin9(B), .pin10(_7400_1_pin3), .pin11(_7400_1_pin11), .pin12(_7400_1_pin6),
    .pin13(_7400_1_pin8), .pin14(1'b1));
  _7400 _7400_2 (
    .pin1(_7400_1_pin11), .pin2(Cin), .pin3(_7400_2_pin3), .pin4(_7400_1_pin11), .pin5(_7400_2_pin3),
    .pin6(_7400_2_pin6), .pin7(1'b0), .pin8(_7400_2_pin8), .pin9(Cin), .pin10(_7400_2_pin3), .pin11(out_4),
    .pin12(_7400_2_pin6), .pin13(_7400_2_pin8), .pin14(1'b1));
  _7400 _7400_3 (
    .pin1(_7400_1_pin3), .pin2(_7400_2_pin3), .pin3(out_5), .pin4(1'b0), .pin5(1'b0), .pin7(1'b0),
    .pin9(1'b0), .pin10(1'b0), .pin12(1'b0), .pin13(1'b0), .pin14(1'b1));  // open: pin6, pin8, pin11

  // Other names for the same wires on the sheet: Cout = out_5; Sum = out_4
endmodule
