// Digital circuit solution.dig as structural Verilog
module solution (
  input  X3,
  input  X2,
  input  X1,
  input  X0,
  output Y1,
  output [4:0] CheckGlitch
);

  wire and_1_out, and_2_out, and_3_out, and_4_out, and_5_out, and_6_out, not_1_out, not_2_out, not_3_out,
       not_4_out;

  not not_1 (not_1_out, X3);
  not not_2 (not_2_out, X2);
  not not_3 (not_3_out, X1);
  not not_4 (not_4_out, X0);
  and and_1 (and_1_out, X0, not_3_out, not_1_out);
  and and_2 (and_2_out, X0, X1, not_2_out, X3);
  and and_3 (and_3_out, X1, X2, not_1_out);
  and and_4 (and_4_out, not_3_out, X2, X3);
  and and_5 (and_5_out, X0, X2, not_1_out);
  and and_6 (and_6_out, X0, not_3_out, X2);
  or or_1 (Y1, and_1_out, and_2_out, and_3_out, and_4_out, and_5_out, and_6_out);
  Counter #(.Bits(5)) counter_1 (.en(1'b1), .C(Y1), .clr(1'b0), .out(CheckGlitch));  // open: ovf

  // Notes on the sheet:
  //   Don't change anything inside this box
endmodule

/* Test case T1:
X3 X2 X1 X0 Y1 CheckGlitch
0  0  0  0  0  0
0  0  0  1  1  1
0  1  0  1  1  1
0  1  1  1  1  1
0  1  0  1  1  1
0  1  0  0  0  1
0  1  0  1  1  2
*/
