// Digital circuit solution.dig as structural Verilog
module solution (
  input  reset,
  input  X,
  input  Y,
  input  Z,
  input  load,
  input  clock,
  output A,
  output B,
  output C
);

  wire [2:0] lookuptable_1_out, multiplexer_1_out;

  LookUpTable #(.Bits(3)) lookuptable_1 (.in0(C), .in1(B), .in2(A), .out(lookuptable_1_out));
  Multiplexer #(.Bits(3)) multiplexer_1 (
    .sel(load), .in_0(lookuptable_1_out), .in_1({X, Y, Z}), .out(multiplexer_1_out));
  D_FF_AS d_ff_as_1 (.Set(reset), .D(multiplexer_1_out[2]), .C(clock), .Clr(1'b0), .Q(A));  // open: nQ
  D_FF_AS d_ff_as_2 (.Set(1'b0), .D(multiplexer_1_out[1]), .C(clock), .Clr(reset), .Q(B));  // open: nQ
  D_FF_AS d_ff_as_3 (.Set(reset), .D(multiplexer_1_out[0]), .C(clock), .Clr(1'b0), .Q(C));  // open: nQ

  // Notes on the sheet:
  //   contents of lookuptable_1 (hex, n*v repeats v):
  //   64,6e,b,0,65,1,b,b
endmodule

/* Test case T01:
X Y Z reset load clock A B C
0 0 0 1     0    0     x x x
0 0 0 1     0    1     1 0 1
0 0 0 0     0    0     1 0 1
0 0 0 0     0    1     0 0 1
0 0 0 0     0    0     0 0 1
0 0 0 0     0    1     1 1 0
0 0 0 0     0    0     1 1 0
0 0 0 0     0    1     0 1 1
0 0 0 0     0    0     0 1 1
0 0 0 0     0    1     0 0 0
0 0 0 0     0    0     0 0 0
1 1 0 0     1    0     0 0 0
1 1 0 0     1    1     1 1 0
1 1 0 0     1    0     1 1 0
0 0 0 0     0    0     1 1 0
0 0 0 0     0    1     0 1 1
0 0 0 0     0    0     0 1 1
0 0 0 0     0    1     0 0 0
0 0 0 0     0    0     0 0 0
0 0 0 0     0    1     1 0 0
0 0 0 0     0    0     1 0 0
0 0 0 1     0    0     1 0 1
0 0 0 0     0    0     1 0 1
0 0 0 0     0    1     0 0 1
0 0 0 0     0    0     0 0 1
0 0 0 0     0    1     1 1 0
0 0 0 0     0    0     1 1 0
0 0 0 0     0    1     0 1 1
0 0 0 0     0    0     0 1 1
0 0 0 0     0    1     0 0 0
0 0 0 1     0    1     1 0 1
0 0 0 0     0    1     1 0 1
0 0 0 0     0    0     1 0 1
0 0 0 0     0    1     0 0 1
0 0 0 0     0    0     0 0 1
0 0 0 0     0    1     1 1 0
0 0 0 0     0    0     1 1 0
0 0 0 0     0    1     0 1 1
0 0 0 0     0    0     0 1 1
0 0 0 0     0    1     0 0 0
0 0 0 0     0    0     0 0 0
0 0 0 0     0    1     1 0 0
0 0 0 0     0    0     1 0 0
0 0 0 0     0    1     1 0 1
0 0 0 0     0    0     1 0 1
*/
