// Digital circuit solution.dig as structural Verilog
module solution (
  input  [15:0] A,
  input  [15:0] D,
  input  [15:0] N,
  input  start,
  input  reset,
  input  clock,
  output [15:0] K,
  output [15:0] S,
  output busy
);

  wire _00, _01, _10, _11, and_2_out, and_4_out, d_ff_2_q, done, finish, load_A, load_K, load_out, load_sum,
       lt, multiplexer_1_out, multiplexer_2_out, multiplexer_3_out, multiplexer_4_out, multiplexer_9_out,
       not_1_out, or_1_out, Qa, st;
  wire [0:0] QaQb;
  wire [15:0] A_n, add_1_s, add_2_s, add_3_s, D_n, K_t, multiplexer_5_out, multiplexer_6_out,
       multiplexer_7_out, N_n, Sum;
  wire [31:0] multiplexer_8_out;

  Multiplexer #(.Selector_Bits(2)) multiplexer_1 (
    .sel({Qa, QaQb[0]}), .in_0(1'b0), .in_1(lt), .in_2(1'b1), .in_3(1'b0), .out(multiplexer_1_out));
  Multiplexer multiplexer_2 (.sel(reset), .in_0(multiplexer_1_out), .in_1(1'b0), .out(multiplexer_2_out));
  D_FF d_ff_1 (.D(multiplexer_2_out), .C(clock), .Q(Qa));  // open: nQ
  Multiplexer multiplexer_3 (.sel(reset), .in_0(start), .in_1(1'b0), .out(multiplexer_3_out));
  Comparator #(.Bits(16)) comparator_1 (.a(Sum), .b(N_n), .lt(lt));  // open: gt, eq
  and and_1 (finish, _01, not_1_out);
  not not_1 (not_1_out, lt);
  D_FF d_ff_2 (.D(multiplexer_3_out), .C(clock), .Q(d_ff_2_q));  // open: nQ
  Add #(.Bits(16)) add_1 (.a(A_n), .b(D_n), .c_i(1'b0), .s(add_1_s));  // open: c_o
  Add #(.Bits(16)) add_2 (.a(A_n), .b(Sum), .c_i(1'b0), .s(add_2_s));  // open: c_o
  Add #(.Bits(16)) add_3 (.a(K_t), .b(16'h1), .c_i(1'b0), .s(add_3_s));  // open: c_o
  and and_2 (and_2_out, ~done, st);  // And
  Multiplexer #(.Selector_Bits(2)) multiplexer_4 (
    .sel({Qa, QaQb[0]}), .in_0(and_2_out), .in_1(1'b0), .in_2(1'b1), .in_3(1'b1), .out(multiplexer_4_out));
  Decoder #(.Selector_Bits(2)) decoder_1 (.sel({Qa, QaQb[0]}), .out_0(_00), .out_1(_01), .out_2(_10), .out_3(_11));
  and and_3 (st, ~d_ff_2_q, start);  // And
  Multiplexer #(.Bits(16)) multiplexer_5 (.sel(_00), .in_0(add_1_s), .in_1(A), .out(multiplexer_5_out));
  Multiplexer #(.Bits(16)) multiplexer_6 (.sel(reset), .in_0(add_2_s), .in_1({16{1'b0}}), .out(multiplexer_6_out));
  Multiplexer #(.Bits(16)) multiplexer_7 (.sel(reset), .in_0(add_3_s), .in_1({16{1'b0}}), .out(multiplexer_7_out));
  Multiplexer #(.Bits(32)) multiplexer_8 (.sel(reset), .in_0({K_t, Sum}), .in_1({32{1'b0}}), .out(multiplexer_8_out));
  Multiplexer multiplexer_9 (.sel(reset), .in_0(multiplexer_4_out), .in_1(1'b0), .out(multiplexer_9_out));
  or or_1 (or_1_out, finish, done);
  D_FF d_ff_3 (.D(multiplexer_9_out), .C(clock), .Q(QaQb[0]));  // open: nQ
  and and_4 (and_4_out, ~reset, or_1_out);  // And
  Register #(.Bits(16)) register_1 (.D(N), .C(clock), .en(_00), .Q(N_n));
  Register #(.Bits(16)) register_2 (.D(multiplexer_5_out), .C(clock), .en(load_A), .Q(A_n));
  Register #(.Bits(16)) register_3 (.D(D), .C(clock), .en(_00), .Q(D_n));
  Register #(.Bits(16)) register_4 (.D(multiplexer_6_out), .C(clock), .en(load_sum), .Q(Sum));
  Register #(.Bits(16)) register_5 (.D(multiplexer_7_out), .C(clock), .en(load_K), .Q(K_t));
  Register #(.Bits(32)) register_6 (.D(multiplexer_8_out), .C(clock), .en(load_out), .Q({K, S}));
  D_FF d_ff_4 (.D(and_4_out), .C(clock), .Q(done));  // open: nQ
  not not_2 (busy, _00);
  or or_2 (load_out, reset, _00);
  or or_3 (load_A, _00, _11);
  or or_4 (load_sum, reset, _10);
  or or_5 (load_K, reset, _11);

  // Other names for the same wires on the sheet: clk = clock; load_D = _00; load_N = _00; out[31:0] = {K, S};
  //   QaQb[1] = Qa; Qb = QaQb[0]; R = reset; S_t = start
endmodule

/* Test case T01:
A D N start reset clock K S busy
0  0  0   0     1     0     x x x
0  0  0   0     1     1     0 0 0
0  0  0   0     0     0     0 0 0
3  2  20  1     0     0     0 0 0
3  2  20  1     0     1     x x 1
3  2  20  0     0     0     x x x
3  2  20  0     0     1     x x x
3  2  20  0     0     0     x x x
3  2  20  0     0     1     x x x
3  2  20  0     0     0     x x x
3  2  20  0     0     1     x x x
3  2  20  0     0     0     x x x
3  2  20  0     0     1     x x x
3  2  20  0     0     0     x x x
3  2  20  0     0     1     x x x
3  2  20  0     0     0     x x x
3  2  20  0     0     1     x x x
3  2  20  0     0     0     x x x
3  2  20  0     0     1     x x x
3  2  20  0     0     0     x x x
3  2  20  0     0     1     x x x
3  2  20  0     0     0     x x x
3  2  20  0     0     1     x x x
3  2  20  0     0     0     x x x
3  2  20  0     0     1     x x x
3  2  20  0     0     0     x x x
3  2  20  0     0     1     x x x
3  2  20  0     0     0     x x x
3  2  20  0     0     1     x x x
3  2  20  0     0     0     x x x
3  2  20  0     0     1     x x x
3  2  20  0     0     0     x x x
3  2  20  0     0     1     x x x
3  2  20  0     0     0     x x x
3  2  20  0     0     1     x x x
3  2  20  0     0     0     x x x
3  2  20  0     0     1     x x x
3  2  20  0     0     0     x x x
3  2  20  0     0     1     x x x
3  2  20  0     0     0     x x x
3  2  20  0     0     1     x x x
3  2  20  0     0     0     x x x
3  2  20  0     0     1     x x x
3  2  20  0     0     0     x x x
3  2  20  0     0     1     x x x
3  2  20  0     0     0     x x x
3  2  20  0     0     1     x x x
3  2  20  0     0     0     x x x
3  2  20  0     0     1     4 24 0
3  2  20  0     0     0     4 24 0
3  2  20  0     0     1     4 24 0
3  2  20  0     0     0     4 24 0
4  3  97  0     0     0     4 24 0
4  3  97  0     0     1     4 24 0
4  3  97  0     0     0     4 24 0
4  3  97  1     0     0     4 24 0
4  3  97  1     0     1     4 24 0
4  3  97  0     0     0     4 24 0
4  3  97  0     0     1     4 24 0
4  3  97  0     0     0     4 24 0
4  3  97  0     0     1     4 24 0
4  3  97  0     0     0     4 24 0
4  3  97  0     0     1     4 24 0
4  3  97  0     0     0     4 24 0
4  3  97  0     1     0     x x x
4  3  97  0     1     1     0 0 0
4  3  97  0     0     0     0 0 0
5  3  60  1     0     0     0 0 0
5  3  60  1     0     1     x x 1
5  3  60  0     0     0     x x x
5  3  60  0     0     1     x x x
5  3  60  0     0     0     x x x
5  3  60  0     0     1     x x x
5  3  60  0     0     0     x x x
5  3  60  0     0     1     x x x
5  3  60  0     0     0     x x x
5  3  60  0     1     0     x x x
5  3  60  0     1     1     0 0 0
5  3  60  0     0     0     0 0 0
5  3  60  0     0     1     0 0 0
5  3  60  0     0     0     0 0 0
5  3  60  0     0     1     0 0 0
5  3  60  0     0     0     0 0 0
1  1  10  1     0     0     0 0 0
1  1  10  1     0     1     x x 1
1  1  10  0     0     0     x x x
1  1  10  0     0     1     x x x
1  1  10  0     0     0     x x x
1  1  10  0     0     1     x x x
1  1  10  0     0     0     x x x
1  1  10  0     0     1     x x x
1  1  10  0     0     0     x x x
1  1  10  0     0     1     x x x
1  1  10  0     0     0     x x x
1  1  10  0     0     1     x x x
1  1  10  0     0     0     x x x
1  1  10  0     0     1     x x x
1  1  10  0     0     0     x x x
1  1  10  0     0     1     x x x
1  1  10  0     0     0     x x x
1  1  10  0     0     1     x x x
1  1  10  0     0     0     x x x
1  1  10  0     0     1     x x x
1  1  10  0     0     0     x x x
1  1  10  0     0     1     x x x
1  1  10  0     0     0     x x x
1  1  10  0     0     1     x x x
1  1  10  0     0     0     x x x
1  1  10  0     0     1     x x x
1  1  10  0     0     0     x x x
1  1  10  0     0     1     x x x
1  1  10  0     0     0     x x x
1  1  10  0     0     1     x x x
1  1  10  0     0     0     x x x
1  1  10  0     0     1     x x x
1  1  10  0     0     0     x x x
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*/
