// Digital circuit solution.dig as structural Verilog
module solution (
  input  [7:0] N,
  input  \new ,
  input  reset,
  input  clock,
  output [7:0] ones,
  output [7:0] odd,
  output busy
);

  wire and_1_out, d_ff_1_q, multiplexer_1_out, multiplexer_8_out, run;
  wire [3:0] bitcount_1_out;
  wire [7:0] add_1_s, add_2_s, multiplexer_2_out, multiplexer_3_out, multiplexer_4_out, multiplexer_5_out,
       multiplexer_6_out, multiplexer_7_out, N_n;

  BitCount #(.Bits(8)) bitcount_1 (.in(multiplexer_5_out), .out(bitcount_1_out));
  Multiplexer multiplexer_1 (.sel(reset), .in_0(\new ), .in_1(1'b0), .out(multiplexer_1_out));
  D_FF d_ff_1 (.D(multiplexer_1_out), .C(clock), .Q(d_ff_1_q));  // open: nQ
  Add #(.Bits(8)) add_1 (.a({4'b0000, bitcount_1_out}), .b(ones), .c_i(1'b0), .s(add_1_s));  // open: c_o
  and and_1 (and_1_out, ~d_ff_1_q, \new );  // And
  Multiplexer #(.Bits(8)) multiplexer_2 (.sel(run), .in_0(N_n), .in_1(N), .out(multiplexer_2_out));
  Add #(.Bits(8)) add_2 (.a(odd), .b({8{1'b0}}), .c_i(bitcount_1_out[0]), .s(add_2_s));  // open: c_o
  Multiplexer #(.Bits(8)) multiplexer_3 (.sel(run), .in_0(ones), .in_1(add_1_s), .out(multiplexer_3_out));
  Multiplexer #(.Bits(8)) multiplexer_4 (.sel(run), .in_0(odd), .in_1(add_2_s), .out(multiplexer_4_out));
  and and_2 (run, ~busy, and_1_out);  // And
  Multiplexer #(.Bits(8)) multiplexer_5 (
    .sel(reset), .in_0(multiplexer_2_out), .in_1({8{1'b0}}), .out(multiplexer_5_out));
  Multiplexer #(.Bits(8)) multiplexer_6 (
    .sel(reset), .in_0(multiplexer_3_out), .in_1({8{1'b0}}), .out(multiplexer_6_out));
  Multiplexer #(.Bits(8)) multiplexer_7 (
    .sel(reset), .in_0(multiplexer_4_out), .in_1({8{1'b0}}), .out(multiplexer_7_out));
  D_FF #(.Bits(8)) d_ff_2 (.D(multiplexer_5_out), .C(clock), .Q(N_n));  // open: nQ
  D_FF #(.Bits(8)) d_ff_3 (.D(multiplexer_6_out), .C(clock), .Q(ones));  // open: nQ
  D_FF #(.Bits(8)) d_ff_4 (.D(multiplexer_7_out), .C(clock), .Q(odd));  // open: nQ
  Multiplexer multiplexer_8 (.sel(reset), .in_0(run), .in_1(1'b0), .out(multiplexer_8_out));
  D_FF d_ff_5 (.D(multiplexer_8_out), .C(clock), .Q(busy));  // open: nQ

  // Other names for the same wires on the sheet: _1_n[7:0] = ones; clk = clock; o_n[7:0] = odd; R = reset
endmodule

/* Test case T2:
N new reset clock ones odd busy
0 0 1 0 x x x
0 0 1 1 0 0 0
0 0 0 0 0 x x
255 1 0 0 x x x
255 1 0 1 x x x
255 0 0 0 x x x
255 0 0 1 8 x x
170 1 0 0 x x x
170 1 0 1 x x x
170 0 0 0 x x x
170 0 0 1 12 x x
1 1 0 0 x x x
1 1 0 1 x x x
1 0 0 0 x x x
1 0 0 1 13 x x
*/

/* Test case T01:
N new reset clock ones odd busy
0   0   1     0     x x x
0   0   1     1     0 0 0
0   0   0     0     0 0 0
5   1   0     0     0 0 0
5   1   0     1     x x 1
5   0   0     0     x x x
5   0   0     1     x x x
5   0   0     0     x x x
5   0   0     1     x x x
5   0   0     0     x x x
5   0   0     1     x x x
5   0   0     0     x x x
5   0   0     1     x x x
5   0   0     0     x x x
5   0   0     1     x x x
5   0   0     0     x x x
5   0   0     1     x x x
5   0   0     0     x x x
5   0   0     1     x x x
5   0   0     0     x x x
5   0   0     1     x x x
5   0   0     0     x x x
5   0   0     1     x x x
5   0   0     0     x x x
5   0   0     1     x x x
5   0   0     0     x x x
5   0   0     1     x x x
5   0   0     0     x x x
5   0   0     1     x x x
5   0   0     0     x x x
5   0   0     1     x x x
5   0   0     0     x x x
5   0   0     1     x x x
5   0   0     0     x x x
5   0   0     1     2 0 0
5   0   0     0     2 0 0
5   0   0     1     2 0 0
5   0   0     0     2 0 0
7   1   0     0     2 0 0
7   1   0     1     x x 1
7   0   0     0     x x x
7   0   0     1     x x x
7   0   0     0     x x x
7   0   0     1     x x x
7   0   0     0     x x x
7   0   0     1     x x x
7   0   0     0     x x x
7   0   0     1     x x x
7   0   0     0     x x x
7   0   0     1     x x x
7   0   0     0     x x x
7   0   0     1     x x x
7   0   0     0     x x x
7   0   0     1     x x x
7   0   0     0     x x x
7   0   0     1     x x x
7   0   0     0     x x x
7   0   0     1     x x x
7   0   0     0     x x x
7   0   0     1     x x x
7   0   0     0     x x x
7   0   0     1     x x x
7   0   0     0     x x x
7   0   0     1     x x x
7   0   0     0     x x x
7   0   0     1     x x x
7   0   0     0     x x x
7   0   0     1     x x x
7   0   0     0     x x x
7   0   0     1     5 1 0
7   0   0     0     5 1 0
7   0   0     1     5 1 0
7   0   0     0     5 1 0
255 1   0     0     5 1 0
255 1   0     1     x x 1
255 0   0     0     x x x
255 0   0     1     x x x
255 0   0     0     x x x
255 0   0     1     x x x
255 0   0     0     x x x
255 0   0     1     x x x
255 0   0     0     x x x
255 0   0     1     x x x
255 0   0     0     x x x
255 0   0     1     x x x
255 0   0     0     x x x
255 0   0     1     x x x
255 0   0     0     x x x
255 0   0     1     x x x
255 0   0     0     x x x
255 0   0     1     x x x
255 0   0     0     x x x
255 0   0     1     x x x
255 0   0     0     x x x
255 0   0     1     x x x
255 0   0     0     x x x
255 0   0     1     x x x
255 0   0     0     x x x
255 0   0     1     x x x
255 0   0     0     x x x
255 0   0     1     x x x
255 0   0     0     x x x
255 0   0     1     x x x
255 0   0     0     x x x
255 0   0     1     13 1 0
255 0   0     0     13 1 0
255 0   0     1     13 1 0
255 0   0     0     13 1 0
0   1   0     0     13 1 0
0   1   0     1     x x 1
0   0   0     0     x x x
0   0   0     1     x x x
0   0   0     0     x x x
0   0   0     1     x x x
0   0   0     0     x x x
0   0   0     1     x x x
0   0   0     0     x x x
0   0   0     1     x x x
0   0   0     0     x x x
0   0   0     1     x x x
0   0   0     0     x x x
0   0   0     1     x x x
0   0   0     0     x x x
0   0   0     1     x x x
0   0   0     0     x x x
0   0   0     1     x x x
0   0   0     0     x x x
0   0   0     1     x x x
0   0   0     0     x x x
0   0   0     1     x x x
0   0   0     0     x x x
0   0   0     1     x x x
0   0   0     0     x x x
0   0   0     1     x x x
0   0   0     0     x x x
0   0   0     1     x x x
0   0   0     0     x x x
0   0   0     1     x x x
0   0   0     0     x x x
0   0   0     1     13 1 0
0   0   0     0     13 1 0
0   0   0     1     13 1 0
0   0   0     0     13 1 0
128 1   0     0     13 1 0
128 1   0     1     x x 1
128 0   0     0     x x x
128 0   0     1     x x x
128 0   0     0     x x x
128 0   0     1     x x x
128 0   0     0     x x x
128 0   0     1     x x x
128 0   0     0     x x x
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*/
