// Digital circuit solution.dig as structural Verilog
module solution (
  input  A,
  input  B,
  output And,
  output Or,
  output Nand,
  output Nor,
  output Xor,
  output Xnor
);

  and and_1 (And, B, A);
  or or_1 (Or, B, A);
  nand nand_1 (Nand, B, A);
  nor nor_1 (Nor, B, A);
  xor xor_1 (Xor, B, A);
  xnor xnor_1 (Xnor, B, A);
endmodule
