// Digital circuit solution.dig as structural Verilog
module solution (
  input  [3:0] In,
  input  [1:0] Selector,
  output [3:0] Output
);

  wire C2, C3, C4, E1, E2, E3, E4, i1__i2__i3, i1_i2__i3_i4, i1_i2__i4, i1_i2_i3, i1_i3__i4, i1_i3_i4,
       i2__i3, i2__i3__i4, i2__i3_i4, i2__i3_i4_t, i2__i4, i2_i3, i2_i3__i4, i2_i3__i4_t, i2_i3_t, i2_i4,
       i2_i4_t, i3__i4, i3__i4_t, i3_i4, i3_i4_t, not_1_out, not_2_out, not_3_out, not_4_out, S1, S2, S3, S4,
       T1, T2, T3;

  not not_1 (not_1_out, In[3]);
  not not_2 (not_2_out, In[2]);
  not not_3 (not_3_out, In[1]);
  not not_4 (not_4_out, In[0]);
  and and_1 (i2_i3__i4, not_2_out, In[1], not_4_out);
  and and_2 (i2_i3__i4_t, In[2], In[1], not_4_out);
  and and_3 (i3__i4, not_3_out, not_4_out);
  and and_4 (i3_i4_t, In[1], In[0]);
  and and_5 (i2_i4, not_2_out, In[0]);
  and and_6 (i2_i4_t, In[2], In[0]);
  and and_7 (i2_i3, not_2_out, In[1]);
  and and_8 (i2__i3, In[2], not_3_out);
  and and_9 (i3__i4_t, In[1], not_4_out);
  and and_10 (i3_i4, not_3_out, In[0]);
  and and_11 (i2__i3_i4_t, In[2], not_3_out, In[0]);
  and and_12 (i2_i3_t, In[2], In[1]);
  and and_13 (i2__i4, In[2], not_4_out);
  and and_14 (i2__i3_i4, not_2_out, not_3_out, In[0]);
  and and_15 (i3_i4_t, In[1], In[0]);
  and and_16 (i2__i3__i4, In[2], not_3_out, not_4_out);
  and and_17 (i1__i2__i3, In[3], not_2_out, not_3_out);
  and and_18 (i1_i2__i3_i4, not_1_out, In[2], not_3_out, In[0]);
  and and_19 (i1_i3_i4, not_1_out, In[1], In[0]);
  and and_20 (i1_i3__i4, not_1_out, In[1], not_4_out);
  and and_21 (i1_i2_i3, not_1_out, In[2], In[1]);
  and and_22 (i1_i2__i4, not_1_out, In[2], not_4_out);
  Multiplexer #(.Selector_Bits(2), .Bits(4)) multiplexer_1 (
    .sel(Selector), .in_0({E1, E2, E3, E4}), .in_1({In[3], C2, C3, C4}), .in_2({T1, T2, T3, In[0]}),
    .in_3({S1, S2, S3, S4}), .out(Output));
  or or_1 (E1, i2_i3__i4_t, i2_i4_t, In[3]);
  or or_2 (E2, i2__i3__i4, i2_i3__i4, i2_i4);
  or or_3 (E3, i3_i4_t, i3__i4);
  or or_4 (E4, i2_i3__i4, i2_i3__i4_t, i3__i4);
  or or_5 (C2, In[2], In[3]);
  or or_6 (C3, i2_i3, i2__i3);
  or or_7 (C4, i3__i4_t, i3_i4);
  or or_8 (T1, i2__i3_i4_t, i2_i3_t, In[3]);
  or or_9 (T2, i2__i4, i2_i3_t, In[3]);
  or or_10 (T3, i2_i3, i2__i3_i4_t, In[3]);
  or or_11 (S1, i1__i2__i3, i1_i2__i3_i4, i1_i3_i4);
  or or_12 (S2, i1_i2_i3, i1_i2__i4, i2__i3_i4);
  or or_13 (S3, i1__i2__i3, i1_i3__i4, i1_i2__i3_i4);
  or or_14 (S4, i2__i3_i4, i1_i2__i3_i4, i1_i3_i4);

  // Other names for the same wires on the sheet: i4 = In[0]; T4 = In[0]; i3 = In[1]; i2 = In[2]; C1 = In[3];
  //   i1 = In[3]; s2_t = Selector[0]; s1_t = Selector[1]
endmodule

/* Test case:
In Selector Output
0 0 3
0 1 0
0 2 0
0 3 0
1 0 4
1 1 1
1 2 1
1 3 5
2 0 5
2 1 3
2 2 2
2 3 2
3 0 6
3 1 2
3 2 3
3 3 9
4 0 7
4 1 6
4 2 4
4 3 4
5 0 8
5 1 7
5 2 11
5 3 11
6 0 9
6 1 5
6 2 12
6 3 6
7 0 10
7 1 4
7 2 13
7 3 13
8 0 11
8 1 12
8 2 14
8 3 10
9 0 12
9 1 13
9 2 15
9 3 15
*/
