// Digital circuit solution.dig as structural Verilog
module solution (
  input  reset,
  input  clk,
  output A,
  output B,
  output C
);

  wire [2:0] multiplexer_1_out, multiplexer_2_out;

  Multiplexer #(.Selector_Bits(3), .Bits(3)) multiplexer_1 (
    .sel({C, B, A}), .in_0(3'b010), .in_1(3'b000), .in_2(3'b011), .in_3(3'b101), .in_4(3'b000),
    .in_5(3'b110), .in_6(3'b000), .in_7(3'b000), .out(multiplexer_1_out));
  Multiplexer #(.Bits(3)) multiplexer_2 (.sel(reset), .in_0(multiplexer_1_out), .in_1(3'b000), .out(multiplexer_2_out));
  D_FF #(.Bits(3)) d_ff_1 (.D(multiplexer_2_out), .C(clk), .Q({C, B, A}));  // open: nQ
endmodule
