// Digital circuit solution.dig as structural Verilog
module solution (
  input  reset,
  input  [1:0] Coin,
  input  clock,
  output Open,
  output [3:0] Change,
  output [1:0] Curr,
  output [1:0] Next
);

  wire and_1_out, and_2_out, and_3_out, and_4_out, and_5_out, and_6_out, and_7_out, and_8_out, and_9_out,
       and_11_out, and_12_out, and_13_out, and_14_out, and_15_out, and_16_out, and_17_out, and_18_out;

  and and_1 (and_1_out, ~reset, ~Coin[1], ~Coin[0], Curr[0]);  // And
  or or_1 (Next[0], and_1_out, and_2_out, and_3_out);
  and and_2 (and_2_out, ~reset, Coin[1], ~Coin[0], ~Curr[1], ~Curr[0]);  // And
  and and_3 (and_3_out, ~reset, ~Coin[1], Coin[0], ~Curr[1], ~Curr[0]);  // And
  and and_4 (and_4_out, ~reset, ~Coin[1], ~Coin[0], Curr[1]);  // And
  and and_5 (and_5_out, ~reset, ~Coin[1], Coin[0], ~Curr[1], Curr[0]);  // And
  or or_2 (Next[1], and_4_out, and_5_out, and_6_out);
  D_FF #(.Bits(2)) d_ff_1 (.D(Next), .C(clock), .Q(Curr));  // open: nQ
  and and_6 (and_6_out, ~reset, Coin[1], ~Coin[0], ~Curr[1], ~Curr[0]);  // And
  and and_7 (and_7_out, ~reset, Coin[1], Curr[0]);  // And
  or or_3 (Open, and_7_out, and_8_out, and_9_out, and_11_out);
  and and_8 (and_8_out, ~reset, Coin[1], Coin[0]);  // And
  and and_9 (and_9_out, ~reset, Coin[1], Curr[1]);  // And
  and and_10 (Change[3], ~reset, Coin[1], Coin[0], Curr[1]);  // And
  and and_11 (and_11_out, ~reset, Coin[0], Curr[1]);  // And
  and and_12 (and_12_out, ~reset, Coin[1], Coin[0], ~Curr[1]);  // And
  or or_4 (Change[2], and_12_out, and_13_out);
  and and_13 (and_13_out, ~reset, Coin[1], ~Coin[0], Curr[1], Curr[0]);  // And
  or or_5 (Change[1], and_14_out, and_15_out);
  and and_14 (and_14_out, ~reset, Coin[1], Coin[0], ~Curr[1], Curr[0]);  // And
  and and_15 (and_15_out, ~reset, Coin[1], ~Coin[0], Curr[1], ~Curr[0]);  // And
  and and_16 (and_16_out, ~reset, Coin[0], Curr[1], Curr[0]);  // And
  and and_17 (and_17_out, ~reset, Coin[1], ~Coin[0], Curr[1], ~Curr[0]);  // And
  or or_6 (Change[0], and_16_out, and_17_out, and_18_out);
  and and_18 (and_18_out, ~reset, Coin[1], ~Coin[0], ~Curr[1], Curr[0]);  // And

  // Other names for the same wires on the sheet: B = Coin[0]; A = Coin[1]; D = Curr[0]; C = Curr[1]
endmodule

/* Test case T14:
reset Coin clock Open Change
1 0 0 x x
1 0 1 x x
1 0 0 0 0
1 0 1 x x
1 0 0 0 0
1 0 1 x x
1 0 0 0 0
1 0 1 x x
0 0 0 0 0
0 0 1 x x
0 0 0 0 0
0 0 1 x x
0 0 0 0 0
0 0 1 x x
0 0 0 0 0
0 0 1 x x
0 0 0 0 0
0 0 1 x x
0 0 0 0 0
0 0 1 x x
0 1 0 0 0
0 1 1 x x
0 1 0 0 0
0 1 1 x x
0 2 0 1 3
0 2 1 x x
0 0 0 0 0
0 0 1 x x
0 0 0 0 0
0 0 1 x x
0 0 0 0 0
0 0 1 x x
0 0 0 0 0
0 0 1 x x
1 0 0 0 0
1 0 1 x x
1 0 0 0 0
1 0 1 x x
0 0 0 0 0
0 0 1 x x
0 0 0 0 0
0 0 1 x x
0 2 0 0 0
0 2 1 x x
0 3 0 1 9
0 3 1 x x
0 0 0 0 0
0 0 1 x x
*/

/* Test case T12:
reset Coin clock Open Change
1 0 0 x x
1 0 1 x x
0 1 0 0 0
0 1 1 x x
1 0 0 0 0
1 0 1 x x
0 0 0 0 0
0 0 1 x x
0 1 0 0 0
0 1 1 x x
0 1 0 0 0
0 1 1 x x
1 0 0 0 0
1 0 1 x x
0 0 0 0 0
0 0 1 x x
0 2 0 0 0
0 2 1 x x
1 0 0 0 0
1 0 1 x x
0 0 0 0 0
0 0 1 x x
0 1 0 0 0
0 1 1 x x
0 1 0 0 0
0 1 1 x x
0 1 0 1 0
0 1 1 x x
0 0 0 0 0
0 0 1 x x
0 2 0 0 0
0 2 1 x x
0 0 0 0 0
0 0 1 x x
1 0 0 0 0
1 0 1 x x
0 3 0 1 4
0 3 1 x x
0 0 0 0 0
0 0 1 x x
*/

/* Test case T10:
reset Coin clock Open Change
1 0 0 x x
1 0 1 x x
0 0 0 0 0
0 0 1 x x
0 0 0 0 0
0 0 1 x x
0 1 0 0 0
0 1 1 x x
0 0 0 0 0
0 0 1 x x
0 0 0 0 0
0 0 1 x x
0 1 0 0 0
0 1 1 x x
0 0 0 0 0
0 0 1 x x
0 0 0 0 0
0 0 1 x x
0 0 0 0 0
0 0 1 x x
0 2 0 1 3
0 2 1 x x
0 0 0 0 0
0 0 1 x x
0 0 0 0 0
0 0 1 x x
0 2 0 0 0
0 2 1 x x
0 0 0 0 0
0 0 1 x x
0 0 0 0 0
0 0 1 x x
0 3 0 1 9
0 3 1 x x
0 0 0 0 0
0 0 1 x x
0 1 0 0 0
0 1 1 x x
0 0 0 0 0
0 0 1 x x
0 2 0 1 1
0 2 1 x x
0 0 0 0 0
0 0 1 x x
0 0 0 0 0
0 0 1 x x
*/

/* Test case T09:
reset Coin clock Open Change
1 0 0 x x
1 0 1 x x
0 1 0 0 0
0 1 1 x x
0 1 0 0 0
0 1 1 x x
0 3 0 1 8
0 3 1 x x
0 0 0 0 0
0 0 1 x x
0 0 0 0 0
0 0 1 x x
*/

/* Test case T07:
reset Coin clock Open Change
1 0 0 x x
1 0 1 x x
0 1 0 0 0
0 1 1 x x
0 1 0 0 0
0 1 1 x x
0 1 0 1 0
0 1 1 x x
0 0 0 0 0
0 0 1 x x
0 0 0 0 0
0 0 1 x x
*/

/* Test case T05:
reset Coin clock Open Change
1 0 0 x x
1 0 1 x x
0 1 0 0 0
0 1 1 x x
0 2 0 1 1
0 2 1 x x
0 0 0 0 0
0 0 1 x x
0 0 0 0 0
0 0 1 x x
*/

/* Test case T02:
reset Coin clock Open Change
1 0 0 x x
1 0 1 x x
0 2 0 0 0
0 2 1 x x
0 1 0 1 1
0 1 1 x x
0 0 0 0 0
0 0 1 x x
0 0 0 0 0
0 0 1 x x
*/

/* Test case T01:
reset Coin clock Open Change
1 0 0 x x
1 0 1 x x
0 3 0 1 4
0 3 1 x x
0 0 0 0 0
0 0 1 x x
0 0 0 0 0
0 0 1 x x
*/
