// Digital circuit solution.dig as structural Verilog
module solution (
  input  reset,
  input  [1:0] Coin,
  input  clock,
  output Open,
  output [3:0] Change,
  output [3:0] S
);

  wire [3:0] multiplexer_6_out, N0, N2, N4, N5, Next;

  Multiplexer #(.Bits(4), .Selector_Bits(2)) multiplexer_1 (
    .sel(Coin), .in_0(4'b0000), .in_1(4'b0010), .in_2(4'b0101), .in_3(4'b1010), .out(N0));
  Multiplexer #(.Selector_Bits(2), .Bits(4)) multiplexer_2 (
    .sel(Coin), .in_0(4'b0010), .in_1(4'b0100), .in_2(4'b0111), .in_3(4'b1100), .out(N2));
  Multiplexer #(.Selector_Bits(2), .Bits(4)) multiplexer_3 (
    .sel(Coin), .in_0(4'b0100), .in_1(4'b0110), .in_2(4'b1001), .in_3(4'b1110), .out(N4));
  Multiplexer #(.Selector_Bits(2), .Bits(4)) multiplexer_4 (
    .sel(Coin), .in_0(4'b0101), .in_1(4'b0111), .in_2(4'b1010), .in_3(4'b1111), .out(N5));
  Multiplexer #(.Selector_Bits(4), .Bits(4)) multiplexer_5 (
    .sel(S), .in_0(N0), .in_1(4'b0000), .in_2(N2), .in_3(4'b0000), .in_4(N4), .in_5(N5), .in_6(4'b0000),
    .in_7(4'b0000), .in_8(4'b0000), .in_9(4'b0000), .in_10(4'b0000), .in_11(4'b0000), .in_12(4'b0000),
    .in_13(4'b0000), .in_14(4'b0000), .in_15(4'b0000), .out(Next));
  Multiplexer #(.Bits(4)) multiplexer_6 (.sel(reset), .in_0(Next), .in_1(4'b0000), .out(multiplexer_6_out));
  Multiplexer #(.Selector_Bits(4), .Bits(5)) multiplexer_7 (
    .sel(S), .in_0({5{1'b0}}), .in_1({5{1'b0}}), .in_2({5{1'b0}}), .in_3({5{1'b0}}), .in_4({5{1'b0}}),
    .in_5({5{1'b0}}), .in_6(5'b10000), .in_7(5'b10001), .in_8(5'b10010), .in_9(5'b10011), .in_10(5'b10100),
    .in_11(5'b10101), .in_12(5'b10110), .in_13(5'b10111), .in_14(5'b11000), .in_15(5'b11001),
    .out({Open, Change}));
  D_FF #(.Bits(4)) d_ff_1 (.D(multiplexer_6_out), .C(clock), .Q(S));  // open: nQ

  // Other names for the same wires on the sheet: Clk = clock; Co[1:0] = Coin; Curr[3:0] = S; R = reset
endmodule

/* Test case T14:
reset Coin clock Open Change S
1 0 0 x x x
1 0 1 0 0 0
1 0 0 x x x
1 0 1 0 0 0
1 0 0 x x x
1 0 1 0 0 0
1 0 0 x x x
1 0 1 0 0 0
0 0 0 0 0 0
0 0 1 0 0 0
0 0 0 0 0 0
0 0 1 0 0 0
0 0 0 0 0 0
0 0 1 0 0 0
0 0 0 0 0 0
0 0 1 0 0 0
0 0 0 0 0 0
0 0 1 0 0 0
0 0 0 0 0 0
0 0 1 0 0 0
0 1 0 0 0 0
0 1 1 0 0 2
0 1 0 0 0 2
0 1 1 0 0 4
0 2 0 0 0 4
0 2 1 1 3 9
0 0 0 1 3 9
0 0 1 0 0 0
0 0 0 0 0 0
0 0 1 0 0 0
0 0 0 0 0 0
0 0 1 0 0 0
0 0 0 0 0 0
0 0 1 0 0 0
1 0 0 x x x
1 0 1 0 0 0
1 0 0 x x x
1 0 1 0 0 0
0 0 0 0 0 0
0 0 1 0 0 0
0 0 0 0 0 0
0 0 1 0 0 0
0 2 0 0 0 0
0 2 1 0 0 5
0 3 0 0 0 5
0 3 1 1 9 15
0 0 0 1 9 15
0 0 1 0 0 0
*/

/* Test case T12:
reset Coin clock Open Change S
1 0 0 x x x
1 0 1 0 0 0
0 1 0 0 0 0
0 1 1 0 0 2
1 0 0 x x x
1 0 1 0 0 0
0 0 0 0 0 0
0 0 1 0 0 0
0 1 0 0 0 0
0 1 1 0 0 2
0 1 0 0 0 2
0 1 1 0 0 4
1 0 0 x x x
1 0 1 0 0 0
0 0 0 0 0 0
0 0 1 0 0 0
0 2 0 0 0 0
0 2 1 0 0 5
1 0 0 x x x
1 0 1 0 0 0
0 0 0 0 0 0
0 0 1 0 0 0
0 1 0 0 0 0
0 1 1 0 0 2
0 1 0 0 0 2
0 1 1 0 0 4
0 1 0 0 0 4
0 1 1 1 0 6
0 0 0 1 0 6
0 0 1 0 0 0
0 2 0 0 0 0
0 2 1 0 0 5
0 0 0 0 0 5
0 0 1 0 0 5
1 0 0 x x x
1 0 1 0 0 0
0 3 0 0 0 0
0 3 1 1 4 10
0 0 0 1 4 10
0 0 1 0 0 0
*/

/* Test case T10:
reset Coin clock Open Change S
1 0 0 x x x
1 0 1 0 0 0
0 0 0 0 0 0
0 0 1 0 0 0
0 0 0 0 0 0
0 0 1 0 0 0
0 1 0 0 0 0
0 1 1 0 0 2
0 0 0 0 0 2
0 0 1 0 0 2
0 0 0 0 0 2
0 0 1 0 0 2
0 1 0 0 0 2
0 1 1 0 0 4
0 0 0 0 0 4
0 0 1 0 0 4
0 0 0 0 0 4
0 0 1 0 0 4
0 0 0 0 0 4
0 0 1 0 0 4
0 2 0 0 0 4
0 2 1 1 3 9
0 0 0 1 3 9
0 0 1 0 0 0
0 0 0 0 0 0
0 0 1 0 0 0
0 2 0 0 0 0
0 2 1 0 0 5
0 0 0 0 0 5
0 0 1 0 0 5
0 0 0 0 0 5
0 0 1 0 0 5
0 3 0 0 0 5
0 3 1 1 9 15
0 0 0 1 9 15
0 0 1 0 0 0
0 1 0 0 0 0
0 1 1 0 0 2
0 0 0 0 0 2
0 0 1 0 0 2
0 2 0 0 0 2
0 2 1 1 1 7
0 0 0 1 1 7
0 0 1 0 0 0
0 0 0 0 0 0
0 0 1 0 0 0
*/

/* Test case T09:
reset Coin clock Open Change S
1 0 0 x x x
1 0 1 0 0 0
0 1 0 0 0 0
0 1 1 0 0 2
0 1 0 0 0 2
0 1 1 0 0 4
0 3 0 0 0 4
0 3 1 1 8 14
0 0 0 1 8 14
0 0 1 0 0 0
0 0 0 0 0 0
0 0 1 0 0 0
*/

/* Test case T07:
reset Coin clock Open Change S
1 0 0 x x x
1 0 1 0 0 0
0 1 0 0 0 0
0 1 1 0 0 2
0 1 0 0 0 2
0 1 1 0 0 4
0 1 0 0 0 4
0 1 1 1 0 6
0 0 0 1 0 6
0 0 1 0 0 0
0 0 0 0 0 0
0 0 1 0 0 0
*/

/* Test case T05:
reset Coin clock Open Change S
1 0 0 x x x
1 0 1 0 0 0
0 1 0 0 0 0
0 1 1 0 0 2
0 2 0 0 0 2
0 2 1 1 1 7
0 0 0 1 1 7
0 0 1 0 0 0
0 0 0 0 0 0
0 0 1 0 0 0
*/

/* Test case T02:
reset Coin clock Open Change S
1 0 0 x x x
1 0 1 0 0 0
0 2 0 0 0 0
0 2 1 0 0 5
0 1 0 0 0 5
0 1 1 1 1 7
0 0 0 1 1 7
0 0 1 0 0 0
0 0 0 0 0 0
0 0 1 0 0 0
*/

/* Test case T01:
reset Coin clock Open Change S
1 0 0 x x x
1 0 1 0 0 0
0 3 0 0 0 0
0 3 1 1 4 10
0 0 0 1 4 10
0 0 1 0 0 0
0 0 0 0 0 0
0 0 1 0 0 0
*/
