// Digital circuit solution.dig as structural Verilog
module solution (
  input  [7:0] A,
  input  [7:0] B,
  input  start,
  input  reset,
  input  clock,
  output [7:0] gcd,
  output busy
);

  wire and_1_out, and_2_out, and_3_out, and_4_out, and_5_out, and_6_out, comparator_1_eq, comparator_1_gt,
       comparator_1_lt, d_ff_4_q, multiplexer_5_out, or_1_out, run;
  wire [7:0] multiplexer_1_out, multiplexer_2_out, multiplexer_3_out, multiplexer_4_out, sub_1_s, sub_2_s, X,
       Xn, Y, Yn;

  Comparator #(.Bits(8)) comparator_1 (.a(X), .b(Y), .gt(comparator_1_gt), .eq(comparator_1_eq), .lt(comparator_1_lt));
  and and_1 (and_1_out, busy, comparator_1_gt);
  and and_2 (and_2_out, busy, comparator_1_eq);
  and and_3 (and_3_out, busy, comparator_1_lt);
  Multiplexer #(.Bits(8)) multiplexer_1 (.sel(and_2_out), .in_0(gcd), .in_1(X), .out(multiplexer_1_out));
  Multiplexer #(.Bits(8)) multiplexer_2 (.sel(run), .in_0(Xn), .in_1(A), .out(multiplexer_2_out));
  Multiplexer #(.Bits(8)) multiplexer_3 (.sel(run), .in_0(Yn), .in_1(B), .out(multiplexer_3_out));
  Multiplexer #(.Bits(8)) multiplexer_4 (
    .sel(reset), .in_0(multiplexer_1_out), .in_1({8{1'b0}}), .out(multiplexer_4_out));
  D_FF #(.Bits(8)) d_ff_1 (.D(multiplexer_4_out), .C(clock), .Q(gcd));  // open: nQ
  D_FF #(.Bits(8)) d_ff_2 (.D(multiplexer_2_out), .C(clock), .Q(X));  // open: nQ
  D_FF #(.Bits(8)) d_ff_3 (.D(multiplexer_3_out), .C(clock), .Q(Y));  // open: nQ
  and and_4 (and_4_out, busy, ~comparator_1_eq);  // And
  Multiplexer multiplexer_5 (.sel(reset), .in_0(start), .in_1(1'b0), .out(multiplexer_5_out));
  or or_1 (or_1_out, run, and_4_out);
  D_FF d_ff_4 (.D(multiplexer_5_out), .C(clock), .Q(d_ff_4_q));  // open: nQ
  Sub #(.Bits(8)) sub_1 (.a(X), .b(Y), .c_i(1'b0), .s(sub_1_s));  // open: c_o
  and and_5 (and_5_out, ~d_ff_4_q, start);  // And
  and and_6 (and_6_out, ~reset, or_1_out);  // And
  Sub #(.Bits(8)) sub_2 (.a(Y), .b(X), .c_i(1'b0), .s(sub_2_s));  // open: c_o
  and and_7 (run, ~busy, and_5_out);  // And
  Multiplexer #(.Bits(8)) multiplexer_6 (.sel(and_1_out), .in_0(X), .in_1(sub_1_s), .out(Xn));
  Multiplexer #(.Bits(8)) multiplexer_7 (.sel(and_3_out), .in_0(Y), .in_1(sub_2_s), .out(Yn));
  D_FF d_ff_5 (.D(and_6_out), .C(clock), .Q(busy));  // open: nQ

  // Other names for the same wires on the sheet: clk = clock; R = reset; S = start

  // Notes on the sheet:
  //   Data path
  //   Control Unit
endmodule

/* Test case T11:
A B start reset clock gcd busy
0 0 0 1 0 x x
0 0 0 1 1 0 0
255 1 1 0 0 x x
255 1 1 0 1 x 1
repeat(20) 255 1 0 0 C x x
255 1 0 1 0 x x
255 1 0 1 1 0 0
255 1 0 0 0 0 0
255 1 0 0 1 0 0
255 1 0 0 0 0 0
255 1 0 0 1 0 0
255 1 0 0 0 0 0
255 1 0 0 1 0 0
18 24 1 0 0 x x
18 24 1 0 1 x 1
repeat(600) 18 24 0 0 C x x
18 24 0 0 0 6 0
18 24 0 0 1 6 0
18 24 0 0 0 6 0
18 24 0 0 1 6 0
18 24 0 1 0 x x
18 24 0 1 1 0 0
18 24 0 1 0 x x
18 24 0 1 1 0 0
18 24 0 0 0 0 0
18 24 0 0 1 0 0
18 24 0 0 0 0 0
18 24 0 0 1 0 0
100 75 1 0 0 x x
100 75 1 0 1 x 1
repeat(600) 100 75 0 0 C x x
100 75 0 0 0 25 0
100 75 0 0 1 25 0
100 75 0 0 0 25 0
100 75 0 0 1 25 0
*/

/* Test case T09:
A B start reset clock gcd busy
0 0 0 1 0 x x
0 0 0 1 1 0 0
84 36 1 0 0 x x
84 36 1 0 1 x 1
repeat(600) 84 36 0 0 C x x
84 36 0 0 0 12 0
84 36 0 0 1 12 0
10 3 0 0 0 12 0
10 3 0 0 1 12 0
10 3 0 0 0 12 0
10 3 0 0 1 12 0
10 3 0 0 0 12 0
10 3 0 0 1 12 0
10 3 0 0 0 12 0
10 3 0 0 1 12 0
10 3 0 0 0 12 0
10 3 0 0 1 12 0
10 3 0 0 0 12 0
10 3 0 0 1 12 0
45 60 1 0 0 x x
45 60 1 0 1 x 1
repeat(600) 45 60 0 0 C x x
45 60 0 0 0 15 0
45 60 0 0 1 15 0
99 1 0 0 0 15 0
99 1 0 0 1 15 0
99 1 0 0 0 15 0
99 1 0 0 1 15 0
99 1 0 0 0 15 0
99 1 0 0 1 15 0
99 1 0 0 0 15 0
99 1 0 0 1 15 0
99 1 0 0 0 15 0
99 1 0 0 1 15 0
99 1 0 0 0 15 0
99 1 0 0 1 15 0
121 11 1 0 0 x x
121 11 1 0 1 x 1
repeat(600) 121 11 0 0 C x x
121 11 0 0 0 11 0
121 11 0 0 1 11 0
7 7 0 0 0 11 0
7 7 0 0 1 11 0
7 7 0 0 0 11 0
7 7 0 0 1 11 0
7 7 0 0 0 11 0
7 7 0 0 1 11 0
7 7 0 0 0 11 0
7 7 0 0 1 11 0
7 7 0 0 0 11 0
7 7 0 0 1 11 0
7 7 0 0 0 11 0
7 7 0 0 1 11 0
*/

/* Test case T07:
A B start reset clock gcd busy
0 0 0 1 0 x x
0 0 0 1 1 0 0
255 1 1 0 0 x x
255 1 1 0 1 x 1
repeat(600) 255 1 0 0 C x x
255 1 0 0 0 1 0
255 1 0 0 1 1 0
255 1 0 0 0 1 0
255 1 0 0 1 1 0
1 255 1 0 0 x x
1 255 1 0 1 x 1
repeat(600) 1 255 0 0 C x x
1 255 0 0 0 1 0
1 255 0 0 1 1 0
1 255 0 0 0 1 0
1 255 0 0 1 1 0
255 254 1 0 0 x x
255 254 1 0 1 x 1
repeat(600) 255 254 0 0 C x x
255 254 0 0 0 1 0
255 254 0 0 1 1 0
255 254 0 0 0 1 0
255 254 0 0 1 1 0
254 255 1 0 0 x x
254 255 1 0 1 x 1
repeat(600) 254 255 0 0 C x x
254 255 0 0 0 1 0
254 255 0 0 1 1 0
254 255 0 0 0 1 0
254 255 0 0 1 1 0
*/

/* Test case T06:
A B start reset clock gcd busy
0 0 0 1 0 x x
0 0 0 1 1 0 0
1 200 1 0 0 x x
1 200 1 0 1 x 1
repeat(600) 1 200 0 0 C x x
1 200 0 0 0 1 0
1 200 0 0 1 1 0
1 200 0 0 0 1 0
1 200 0 0 1 1 0
200 1 1 0 0 x x
200 1 1 0 1 x 1
repeat(600) 200 1 0 0 C x x
200 1 0 0 0 1 0
200 1 0 0 1 1 0
200 1 0 0 0 1 0
200 1 0 0 1 1 0
2 1 1 0 0 x x
2 1 1 0 1 x 1
repeat(600) 2 1 0 0 C x x
2 1 0 0 0 1 0
2 1 0 0 1 1 0
2 1 0 0 0 1 0
2 1 0 0 1 1 0
*/

/* Test case T05:
A B start reset clock gcd busy
0 0 0 1 0 x x
0 0 0 1 1 0 0
84 36 1 0 0 x x
84 36 1 0 1 x 1
repeat(600) 84 36 0 0 C x x
84 36 0 0 0 12 0
84 36 0 0 1 12 0
84 36 0 0 0 12 0
84 36 0 0 1 12 0
36 84 1 0 0 x x
36 84 1 0 1 x 1
repeat(600) 36 84 0 0 C x x
36 84 0 0 0 12 0
36 84 0 0 1 12 0
36 84 0 0 0 12 0
36 84 0 0 1 12 0
120 75 1 0 0 x x
120 75 1 0 1 x 1
repeat(600) 120 75 0 0 C x x
120 75 0 0 0 15 0
120 75 0 0 1 15 0
120 75 0 0 0 15 0
120 75 0 0 1 15 0
*/

/* Test case T02:
A B start reset clock gcd busy
0 0 0 1 0 x x
0 0 0 1 1 0 0
48 12 1 0 0 x x
48 12 1 0 1 x 1
repeat(600) 48 12 0 0 C x x
48 12 0 0 0 12 0
48 12 0 0 1 12 0
48 12 0 0 0 12 0
48 12 0 0 1 12 0
255 5 1 0 0 x x
255 5 1 0 1 x 1
repeat(600) 255 5 0 0 C x x
255 5 0 0 0 5 0
255 5 0 0 1 5 0
255 5 0 0 0 5 0
255 5 0 0 1 5 0
128 2 1 0 0 x x
128 2 1 0 1 x 1
repeat(600) 128 2 0 0 C x x
128 2 0 0 0 2 0
128 2 0 0 1 2 0
128 2 0 0 0 2 0
128 2 0 0 1 2 0
*/

/* Test case T01:
A B start reset clock gcd busy
0 0 0 1 0 x x
0 0 0 1 1 0 0
12 12 1 0 0 x x
12 12 1 0 1 x 1
repeat(600) 12 12 0 0 C x x
12 12 0 0 0 12 0
12 12 0 0 1 12 0
12 12 0 0 0 12 0
12 12 0 0 1 12 0
200 200 1 0 0 x x
200 200 1 0 1 x 1
repeat(600) 200 200 0 0 C x x
200 200 0 0 0 200 0
200 200 0 0 1 200 0
200 200 0 0 0 200 0
200 200 0 0 1 200 0
1 1 1 0 0 x x
1 1 1 0 1 x 1
repeat(600) 1 1 0 0 C x x
1 1 0 0 0 1 0
1 1 0 0 1 1 0
1 1 0 0 0 1 0
1 1 0 0 1 1 0
*/
