// Digital circuit solution_2.dig as structural Verilog
module solution_2 (
  input  reset,
  input  [15:0] P,
  input  start,
  input  clock,
  output [15:0] W,
  output [15:0] H,
  output [31:0] A,
  output busy,
  output [15:0] out_9,
  output [15:0] out_10,
  output [15:0] out_11,
  output [15:0] out_12
);

  wire _000, _001, _010, _011, _100, _101, _110, _111, d_ff_2_q, gt, load_h, load_out, load_p, load_w,
       multiplexer_1_out, multiplexer_2_out, multiplexer_3_out, multiplexer_4_out, multiplexer_5_out,
       multiplexer_12_out, multiplexer_13_out, Qa, st;
  wire [1:0] QaQbQc;
  wire [15:0] add_1_s, div_1_q, multiplexer_7_out, multiplexer_8_out, multiplexer_9_out, multiplexer_10_out,
       sub_1_s, sub_2_s;
  wire [31:0] mul_1_mul;
  wire [63:0] multiplexer_11_out;

  Multiplexer #(.Selector_Bits(3)) multiplexer_1 (
    .sel({Qa, QaQbQc}), .in_0(1'b0), .in_1(1'b0), .in_2(1'b0), .in_3(1'b1), .in_4(1'b0), .in_5(1'b0),
    .in_6(1'b0), .in_7(1'b0), .out(multiplexer_1_out));
  Multiplexer multiplexer_2 (.sel(reset), .in_0(multiplexer_1_out), .in_1(1'b0), .out(multiplexer_2_out));
  D_FF d_ff_1 (.D(multiplexer_2_out), .C(clock), .Q(Qa));  // open: nQ
  Multiplexer #(.Selector_Bits(3)) multiplexer_3 (
    .sel({Qa, QaQbQc}), .in_0(1'b0), .in_1(1'b1), .in_2(gt), .in_3(1'b0), .in_4(1'b1), .in_5(1'b0),
    .in_6(1'b0), .in_7(1'b0), .out(multiplexer_3_out));
  Multiplexer multiplexer_4 (.sel(reset), .in_0(start), .in_1(1'b0), .out(multiplexer_4_out));
  Div #(.Bits(16)) div_1 (.a(out_9), .b(16'h2), .q(div_1_q));  // open: r
  Multiplexer multiplexer_5 (.sel(reset), .in_0(multiplexer_3_out), .in_1(1'b0), .out(multiplexer_5_out));
  D_FF d_ff_2 (.D(multiplexer_4_out), .C(clock), .Q(d_ff_2_q));  // open: nQ
  Sub #(.Bits(16)) sub_1 (.a(out_10), .b(16'h1), .c_i(1'b0), .s(sub_1_s));  // open: c_o
  Sub #(.Bits(16)) sub_2 (.a(div_1_q), .b(16'h1), .c_i(1'b0), .s(sub_2_s));  // open: c_o
  Add #(.Bits(16)) add_1 (.a(out_11), .b(16'h1), .c_i(1'b0), .s(add_1_s));  // open: c_o
  D_FF d_ff_3 (.D(multiplexer_5_out), .C(clock), .Q(QaQbQc[1]));  // open: nQ
  Decoder #(.Selector_Bits(3)) decoder_1 (
    .sel({Qa, QaQbQc}), .out_0(_000), .out_1(_001), .out_2(_010), .out_3(_011), .out_4(_100), .out_5(_101),
    .out_6(_110), .out_7(_111));
  Multiplexer #(.Bits(16)) multiplexer_6 (.sel(_001), .in_0(sub_1_s), .in_1(sub_2_s), .out(out_12));
  Multiplexer #(.Bits(16)) multiplexer_7 (.sel(_001), .in_0(add_1_s), .in_1(16'h1), .out(multiplexer_7_out));
  Mul #(.Bits(16)) mul_1 (.a(out_10), .b(out_11), .mul(mul_1_mul));
  and and_1 (st, ~d_ff_2_q, start);  // And
  Multiplexer #(.Bits(16)) multiplexer_8 (.sel(reset), .in_0(P), .in_1({16{1'b0}}), .out(multiplexer_8_out));
  Multiplexer #(.Bits(16)) multiplexer_9 (.sel(reset), .in_0(out_12), .in_1({16{1'b0}}), .out(multiplexer_9_out));
  Multiplexer #(.Bits(16)) multiplexer_10 (
    .sel(reset), .in_0(multiplexer_7_out), .in_1({16{1'b0}}), .out(multiplexer_10_out));
  Multiplexer #(.Bits(64)) multiplexer_11 (
    .sel(reset), .in_0({mul_1_mul, out_11, out_10}), .in_1({64{1'b0}}), .out(multiplexer_11_out));
  Multiplexer #(.Selector_Bits(3)) multiplexer_12 (
    .sel({Qa, QaQbQc}), .in_0(st), .in_1(1'b0), .in_2(gt), .in_3(1'b0), .in_4(1'b0), .in_5(1'b0),
    .in_6(1'b0), .in_7(1'b0), .out(multiplexer_12_out));
  Register #(.Bits(16)) register_1 (.D(multiplexer_8_out), .C(clock), .en(load_p), .Q(out_9));
  Register #(.Bits(16)) register_2 (.D(multiplexer_9_out), .C(clock), .en(load_w), .Q(out_10));
  Register #(.Bits(16)) register_3 (.D(multiplexer_10_out), .C(clock), .en(load_h), .Q(out_11));
  Register #(.Bits(64)) register_4 (.D(multiplexer_11_out), .C(clock), .en(load_out), .Q({A, W, H}));
  Multiplexer multiplexer_13 (.sel(reset), .in_0(multiplexer_12_out), .in_1(1'b0), .out(multiplexer_13_out));
  D_FF d_ff_4 (.D(multiplexer_13_out), .C(clock), .Q(QaQbQc[0]));  // open: nQ
  Comparator #(.Bits(16)) comparator_1 (.a(out_10), .b(out_11), .gt(gt));  // open: eq, lt
  or or_1 (load_out, _000, reset);
  or or_2 (load_w, _001, _011, reset);
  or or_3 (load_h, _001, _100, reset);
  or or_4 (load_p, _000, reset);
  not not_1 (busy, _000);

  // Other names for the same wires on the sheet: clk = clock; H_n[15:0] = out_11; P_n[15:0] = out_9; QaQbQc[2] = Qa;
  //   Qb = QaQbQc[1]; Qc = QaQbQc[0]; R = reset; S = start; W_n[15:0] = out_10
endmodule

/* Test case T2:
P start clock reset W H A busy
0 0 0 1 x x x x
0 0 1 1 x x x x
0 0 0 0 0 0 0 0
0 0 1 0 0 0 0 0
3819 1 0 0 x x x x
3819 1 1 0 x x x x
0 0 0 0 x x x x
0 0 1 0 x x x x
0 0 0 0 x x x x
0 0 1 0 x x x x
0 0 0 0 x x x x
0 0 1 0 x x x x
0 0 0 0 x x x x
0 0 1 0 x x x x
0 0 0 0 x x x x
0 0 1 0 x x x x
0 0 0 0 x x x x
0 0 1 0 x x x x
0 0 0 0 x x x x
0 0 1 0 x x x x
0 0 0 0 x x x x
0 0 1 0 x x x x
0 0 0 0 x x x x
0 0 1 0 x x x x
0 0 0 0 x x x x
0 0 1 0 x x x x
0 0 0 0 x x x x
0 0 1 0 x x x x
0 0 0 0 x x x x
0 0 1 0 x x x x
0 0 0 0 x x x x
0 0 1 0 x x x x
0 0 0 0 x x x x
0 0 1 0 x x x x
0 0 0 0 x x x x
0 0 1 0 x x x x
0 0 0 0 x x x x
0 0 1 0 x x x x
0 0 0 0 x x x x
0 0 1 0 x x x x
0 0 0 0 x x x x
0 0 1 0 x x x x
0 0 0 0 x x x x
0 0 1 0 x x x x
0 0 0 0 x x x x
0 0 1 0 x x x x
0 0 0 0 x x x x
0 0 1 0 x x x x
0 0 0 0 x x x x
0 0 1 0 x x x x
0 0 0 0 x x x x
0 0 1 0 x x x x
0 0 0 0 x x x x
0 0 1 0 x x x x
0 0 0 0 x x x x
0 0 1 0 x x x x
0 0 0 0 x x x x
0 0 1 0 x x x x
0 0 0 0 x x x x
0 0 1 0 x x x x
0 0 0 0 x x x x
0 0 1 0 x x x x
0 0 0 0 x x x x
0 0 1 0 x x x x
0 0 0 0 x x x x
0 0 1 0 x x x x
0 0 0 0 x x x x
0 0 1 0 x x x x
0 0 0 0 x x x x
0 0 1 0 x x x x
0 0 0 0 x x x x
0 0 1 0 x x x x
0 0 0 0 x x x x
0 0 1 0 x x x x
0 0 0 0 x x x x
0 0 1 0 x x x x
0 0 0 0 x x x x
0 0 1 0 x x x x
0 0 0 0 x x x x
0 0 1 0 x x x x
0 0 0 0 x x x x
0 0 1 0 x x x x
0 0 0 0 x x x x
0 0 1 0 x x x x
0 0 0 0 x x x x
0 0 1 0 x x x x
0 0 0 0 x x x x
0 0 1 0 x x x x
0 0 0 0 x x x x
0 0 1 0 x x x x
0 0 0 0 x x x x
0 0 1 0 x x x x
0 0 0 0 x x x x
0 0 1 0 x x x x
0 0 0 0 x x x x
0 0 1 0 x x x x
0 0 0 0 x x x x
0 0 1 0 x x x x
0 0 0 0 x x x x
0 0 1 0 x x x x
0 0 0 0 x x x x
*/

/* Test case T01:
P start clock reset W H A busy
0 0 0 1 x x x x
0 0 1 1 x x x x
0 0 0 0 0 0 0 0
0 0 1 0 0 0 0 0
92 1 0 0 x x x x
92 1 1 0 x x x x
0 0 0 0 x x x x
0 0 1 0 x x x x
0 0 0 0 x x x x
0 0 1 0 x x x x
0 0 0 0 x x x x
0 0 1 0 x x x x
0 0 0 0 x x x x
0 0 1 0 x x x x
0 0 0 0 x x x x
0 0 1 0 x x x x
0 0 0 0 x x x x
0 0 1 0 x x x x
0 0 0 0 x x x x
0 0 1 0 x x x x
0 0 0 0 x x x x
0 0 1 0 x x x x
0 0 0 0 x x x x
0 0 1 0 x x x x
0 0 0 0 x x x x
0 0 1 0 x x x x
0 0 0 0 x x x x
0 0 1 0 x x x x
0 0 0 0 x x x x
0 0 1 0 x x x x
0 0 0 0 x x x x
0 0 1 0 x x x x
0 0 0 0 x x x x
0 0 1 0 x x x x
0 0 0 0 x x x x
0 0 1 0 x x x x
0 0 0 0 x x x x
0 0 1 0 x x x x
0 0 0 0 x x x x
0 0 1 0 x x x x
0 0 0 0 x x x x
0 0 1 0 x x x x
0 0 0 0 x x x x
0 0 1 0 x x x x
0 0 0 0 x x x x
0 0 1 0 x x x x
0 0 0 0 x x x x
0 0 1 0 x x x x
0 0 0 0 x x x x
0 0 1 0 x x x x
0 0 0 0 x x x x
0 0 1 0 x x x x
0 0 0 0 x x x x
0 0 1 0 x x x x
0 0 0 0 x x x x
0 0 1 0 x x x x
0 0 0 0 x x x x
0 0 1 0 x x x x
0 0 0 0 x x x x
0 0 1 0 x x x x
0 0 0 0 x x x x
0 0 1 0 x x x x
0 0 0 0 x x x x
0 0 1 0 x x x x
0 0 0 0 x x x x
0 0 1 0 x x x x
0 0 0 0 x x x x
0 0 1 0 x x x x
0 0 0 0 x x x x
0 0 1 0 x x x x
0 0 0 0 x x x x
0 0 1 0 x x x x
0 0 0 0 x x x x
0 0 1 0 x x x x
0 0 0 0 x x x x
0 0 1 0 x x x x
0 0 0 0 x x x x
0 0 1 0 x x x x
0 0 0 0 x x x x
0 0 1 0 x x x x
0 0 0 0 x x x x
0 0 1 0 x x x x
0 0 0 0 x x x x
0 0 1 0 x x x x
0 0 0 0 x x x x
0 0 1 0 x x x x
0 0 0 0 x x x x
0 0 1 0 x x x x
0 0 0 0 x x x x
0 0 1 0 x x x x
0 0 0 0 x x x x
0 0 1 0 x x x x
0 0 0 0 x x x x
0 0 1 0 x x x x
0 0 0 0 x x x x
0 0 1 0 x x x x
0 0 0 0 x x x x
0 0 1 0 x x x x
0 0 0 0 x x x x
0 0 1 0 x x x x
0 0 0 0 x x x x
0 0 1 0 x x x x
0 0 0 0 x x x x
0 0 1 0 x x x x
0 0 0 0 x x x x
0 0 1 0 x x x x
0 0 0 0 x x x x
0 0 1 0 x x x x
0 0 0 0 x x x x
0 0 1 0 x x x x
0 0 0 0 x x x x
0 0 1 0 x x x x
0 0 0 0 x x x x
0 0 1 0 x x x x
0 0 0 0 x x x x
0 0 1 0 x x x x
0 0 0 0 x x x x
0 0 1 0 x x x x
0 0 0 0 x x x x
0 0 1 0 x x x x
0 0 0 0 x x x x
0 0 1 0 x x x x
0 0 0 0 x x x x
0 0 1 0 x x x x
0 0 0 0 x x x x
0 0 1 0 x x x x
0 0 0 0 x x x x
0 0 1 0 x x x x
0 0 0 0 x x x x
0 0 1 0 x x x x
0 0 0 0 x x x x
0 0 1 0 x x x x
0 0 0 0 x x x x
0 0 1 0 x x x x
0 0 0 0 x x x x
0 0 1 0 x x x x
0 0 0 0 x x x x
0 0 1 0 x x x x
0 0 0 0 x x x x
0 0 1 0 x x x x
0 0 0 0 x x x x
0 0 1 0 x x x x
0 0 0 0 x x x x
0 0 1 0 x x x x
0 0 0 0 x x x x
0 0 1 0 x x x x
0 0 0 0 x x x x
0 0 1 0 x x x x
0 0 0 0 x x x x
0 0 1 0 x x x x
0 0 0 0 x x x x
0 0 1 0 x x x x
0 0 0 0 x x x x
0 0 1 0 x x x x
0 0 0 0 x x x x
0 0 1 0 x x x x
0 0 0 0 x x x x
0 0 1 0 x x x x
0 0 0 0 x x x x
0 0 1 0 x x x x
0 0 0 0 x x x x
0 0 1 0 x x x x
0 0 0 0 x x x x
0 0 1 0 x x x x
0 0 0 0 x x x x
0 0 1 0 x x x x
0 0 0 0 x x x x
0 0 1 0 x x x x
0 0 0 0 x x x x
0 0 1 0 x x x x
0 0 0 0 x x x x
0 0 1 0 x x x x
0 0 0 0 x x x x
0 0 1 0 x x x x
0 0 0 0 x x x x
0 0 1 0 x x x x
0 0 0 0 x x x x
0 0 1 0 x x x x
0 0 0 0 x x x x
0 0 1 0 x x x x
0 0 0 0 x x x x
0 0 1 0 x x x x
0 0 0 0 x x x x
0 0 1 0 x x x x
0 0 0 0 x x x x
0 0 1 0 x x x x
0 0 0 0 x x x x
0 0 1 0 x x x x
0 0 0 0 x x x x
0 0 1 0 x x x x
0 0 0 0 x x x x
0 0 1 0 x x x x
0 0 0 0 x x x x
0 0 1 0 x x x x
0 0 0 0 x x x x
0 0 1 0 x x x x
0 0 0 0 x x x x
0 0 1 0 x x x x
0 0 0 0 x x x x
0 0 1 0 x x x x
0 0 0 0 x x x x
0 0 1 0 x x x x
0 0 0 0 x x x x
0 0 1 0 x x x x
0 0 0 0 x x x x
0 0 1 0 x x x x
0 0 0 0 x x x x
0 0 1 0 x x x x
0 0 0 0 x x x x
0 0 1 0 x x x x
0 0 0 0 x x x x
0 0 1 0 x x x x
0 0 0 0 x x x x
0 0 1 0 x x x x
0 0 0 0 x x x x
0 0 1 0 x x x x
0 0 0 0 x x x x
0 0 1 0 x x x x
0 0 0 0 x x x x
0 0 1 0 x x x x
0 0 0 0 x x x x
0 0 1 0 x x x x
0 0 0 0 x x x x
0 0 1 0 x x x x
0 0 0 0 x x x x
0 0 1 0 x x x x
0 0 0 0 x x x x
0 0 1 0 x x x x
0 0 0 0 x x x x
0 0 1 0 x x x x
0 0 0 0 x x x x
0 0 1 0 x x x x
0 0 0 0 x x x x
0 0 1 0 x x x x
0 0 0 0 x x x x
0 0 1 0 x x x x
0 0 0 0 x x x x
0 0 1 0 x x x x
0 0 0 0 x x x x
0 0 1 0 x x x x
0 0 0 0 x x x x
0 0 1 0 x x x x
0 0 0 0 x x x x
0 0 1 0 x x x x
0 0 0 0 x x x x
0 0 1 0 x x x x
0 0 0 0 x x x x
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*/
